// Logisim project RISCV_SIMD.circ as structural Verilog
module main (
  input  [4:0] in_1,
  output [31:0] out_2
);

  wire aluc_1_zero, branch_ctrl_1_pcsrc, button_1_out, button_2_out, clock_1_out, control_1_alusrc,
       control_1_auipc, control_1_jalr, control_1_lui, control_1_memread, control_1_memtoreg,
       control_1_memwrite, control_1_regwrite, ex_mem_1_memread_o, ex_mem_1_memtoreg_o, ex_mem_1_memwrite_o,
       ex_mem_1_regwrite_o, ex_mem_1_zero_o, hazard_unit_1_flush, hazard_unit_1_ifidwrite, hazard_unit_1_nop,
       hazard_unit_1_pcwrite, id_ex_1_alusrc_o, id_ex_1_func7_o, id_ex_1_lui_o, id_ex_1_memread_o,
       id_ex_1_memtoreg_o, id_ex_1_memwrite_o, id_ex_1_regwrite_o, if_id_1_flush_next, mem_wb_1_memtoreg_o,
       mem_wb_1_regwrite_o, or_1_out;
  wire [1:0] control_1_aluop, control_1_branch, ex_mem_1_branch_o, forwarding_unit_1_fora,
       forwarding_unit_1_forb, id_ex_1_aluop_o, id_ex_1_branch_o, id_ex_1_vec_size_o;
  wire [2:0] id_ex_1_func3_o;
  wire [3:0] alu_ctrl_1_aluctrl;
  wire [4:0] ex_mem_1_rw_o, id_ex_1_ra1_o, id_ex_1_ra2_o, id_ex_1_rw_o, mem_wb_1_rw_o,
       regadress_validator_1_ra1_o, regadress_validator_1_ra2_o;
  wire [31:0] aluc_1_r, data_mem_dout, ex_mem_1_alu_res_o, ex_mem_1_branch_res_o, ex_mem_1_rd2_o,
       id_ex_1_imm_o, id_ex_1_pc_o, id_ex_1_pcnext_o, id_ex_1_rd1_o, id_ex_1_rd2_o, if_id_1_instruc_o,
       if_id_1_pc_o, if_id_1_pcnext_o, imm_gen_1_imm, Instruction_mem_data, mem_wb_1_alu_res_o,
       mem_wb_1_rdm_o, multiplexer_1_out, multiplexer_2_out, multiplexer_3_out, multiplexer_4_out,
       multiplexer_5_out, multiplexer_6_out, multiplexer_7_out, multiplexer_8_out, multiplexer_9_out, pc_1_b,
       reg_file_1_rd1, reg_file_1_rd2, somador_1_s, somador_2_s;

  Clock clock_1 (.out(clock_1_out));
  Button button_1 (.out(button_1_out));
  Multiplexer #(.width(32)) multiplexer_1 (
    .in0(somador_1_s), .in1(ex_mem_1_branch_res_o), .out(multiplexer_1_out), .sel(branch_ctrl_1_pcsrc));
  PC pc_1 (
    .clock(clock_1_out), .reset(button_1_out), .write_e(hazard_unit_1_pcwrite), .a(multiplexer_1_out),
    .b(pc_1_b));
  ROM #(.addrWidth(24), .dataWidth(32)) Instruction_mem (.addr(pc_1_b[23:0]), .data(Instruction_mem_data));
  Somador somador_1 (.A(pc_1_b), .B_u(32'h1), .S(somador_1_s));
  Button button_2 (.out(button_2_out));
  IF_ID if_id_1 (
    .pc(pc_1_b), .instruc(Instruction_mem_data), .clock(clock_1_out), .write_e(hazard_unit_1_ifidwrite),
    .flush(hazard_unit_1_flush), .pcnext(somador_1_s), .pc_o(if_id_1_pc_o), .instruc_o(if_id_1_instruc_o),
    .flush_next(if_id_1_flush_next), .pcnext_o(if_id_1_pcnext_o));
  Reg_file reg_file_1 (
    .clock(clock_1_out), .write_e(mem_wb_1_regwrite_o), .reset(button_2_out),
    .rd1a(if_id_1_instruc_o[19:15]), .rd2a(if_id_1_instruc_o[24:20]), .rwa(mem_wb_1_rw_o),
    .manual_address(in_1), .rw(multiplexer_9_out), .rd1(reg_file_1_rd1), .rd2(reg_file_1_rd2),
    .manual_value(out_2));
  Imm_gen imm_gen_1 (.instruc(if_id_1_instruc_o), .imm(imm_gen_1_imm));
  RegAdress_Validator regadress_validator_1 (
    .ra1(if_id_1_instruc_o[19:15]), .ra2(if_id_1_instruc_o[24:20]), .opcode(if_id_1_instruc_o[6:0]),
    .ra1_o(regadress_validator_1_ra1_o), .ra2_o(regadress_validator_1_ra2_o));
  Multiplexer #(.width(32)) multiplexer_2 (
    .in0(if_id_1_pc_o), .in1(reg_file_1_rd1), .out(multiplexer_2_out), .sel(control_1_jalr));
  Multiplexer #(.width(32)) multiplexer_3 (
    .in0(reg_file_1_rd1), .in1(if_id_1_pc_o), .out(multiplexer_3_out), .sel(control_1_auipc));
  Hazard_unit hazard_unit_1 (
    .idexmemread(id_ex_1_memread_o), .rwa(id_ex_1_rw_o), .rda1(if_id_1_instruc_o[19:15]),
    .rda2(if_id_1_instruc_o[19:15]), .branch(branch_ctrl_1_pcsrc), .pcwrite(hazard_unit_1_pcwrite),
    .ifidwrite(hazard_unit_1_ifidwrite), .nop(hazard_unit_1_nop), .flush(hazard_unit_1_flush));
  or or_1 (or_1_out, hazard_unit_1_flush, if_id_1_flush_next);
  Control control_1 (
    .opcode(if_id_1_instruc_o[6:0]), .nop(hazard_unit_1_nop), .func3(if_id_1_instruc_o[14:12]),
    .regwrite(control_1_regwrite), .alusrc(control_1_alusrc), .memread(control_1_memread),
    .memwrite(control_1_memwrite), .memtoreg(control_1_memtoreg), .lui(control_1_lui),
    .aluop(control_1_aluop), .branch(control_1_branch), .jalr(control_1_jalr), .auipc(control_1_auipc));
  ID_EX id_ex_1 (
    .clock(clock_1_out), .imm(imm_gen_1_imm), .rd1(multiplexer_3_out), .rd2(reg_file_1_rd2),
    .pc(multiplexer_2_out), .func3(if_id_1_instruc_o[14:12]), .rw(if_id_1_instruc_o[11:7]),
    .regwrite(control_1_regwrite), .alusrc(control_1_alusrc), .memread(control_1_memread),
    .memwrite(control_1_memwrite), .memtoreg(control_1_memtoreg), .lui(control_1_lui),
    .aluop(control_1_aluop), .branch(control_1_branch), .func7(if_id_1_instruc_o[30]),
    .ra1(regadress_validator_1_ra1_o), .ra2(regadress_validator_1_ra2_o), .flush(or_1_out),
    .vec_size(if_id_1_instruc_o[1:0]), .pcnext(if_id_1_pcnext_o), .imm_o(id_ex_1_imm_o),
    .rd1_o(id_ex_1_rd1_o), .rd2_o(id_ex_1_rd2_o), .pc_o(id_ex_1_pc_o), .func3_o(id_ex_1_func3_o),
    .rw_o(id_ex_1_rw_o), .regwrite_o(id_ex_1_regwrite_o), .alusrc_o(id_ex_1_alusrc_o),
    .memread_o(id_ex_1_memread_o), .memwrite_o(id_ex_1_memwrite_o), .memtoreg_o(id_ex_1_memtoreg_o),
    .lui_o(id_ex_1_lui_o), .aluop_o(id_ex_1_aluop_o), .branch_o(id_ex_1_branch_o), .func7_o(id_ex_1_func7_o),
    .ra1_o(id_ex_1_ra1_o), .ra2_o(id_ex_1_ra2_o), .vec_size_o(id_ex_1_vec_size_o), .pcnext_o(id_ex_1_pcnext_o));
  Multiplexer #(.width(32)) multiplexer_4 (
    .in0(id_ex_1_rd1_o), .in1({32{1'b0}}), .out(multiplexer_4_out), .sel(id_ex_1_lui_o));
  Multiplexer #(.width(32)) multiplexer_5 (
    .in0(id_ex_1_rd2_o), .in1(id_ex_1_imm_o), .out(multiplexer_5_out), .sel(id_ex_1_alusrc_o));
  Multiplexer #(.select(2), .width(32)) multiplexer_6 (
    .in0(multiplexer_4_out), .in1(multiplexer_9_out), .in2(ex_mem_1_alu_res_o), .out(multiplexer_6_out),
    .sel(forwarding_unit_1_fora));  // open: in3
  Multiplexer #(.select(2), .width(32)) multiplexer_7 (
    .in0(multiplexer_5_out), .in1(multiplexer_9_out), .in2(ex_mem_1_alu_res_o), .out(multiplexer_7_out),
    .sel(forwarding_unit_1_forb));  // open: in3
  ALU_ctrl alu_ctrl_1 (
    .func7(id_ex_1_func7_o), .func3(id_ex_1_func3_o), .aluop(id_ex_1_aluop_o), .aluctrl(alu_ctrl_1_aluctrl));
  ALUc aluc_1 (
    .a(multiplexer_6_out), .b(multiplexer_7_out), .Vec_size(id_ex_1_vec_size_o), .op(alu_ctrl_1_aluctrl),
    .zero(aluc_1_zero), .r(aluc_1_r));
  Somador somador_2 (.A(id_ex_1_pc_o), .B_u(id_ex_1_imm_o), .S(somador_2_s));
  Multiplexer #(.select(2), .width(32)) multiplexer_8 (
    .in0(aluc_1_r), .in1(aluc_1_r), .in2(aluc_1_r), .in3(id_ex_1_pcnext_o), .out(multiplexer_8_out),
    .sel(id_ex_1_branch_o));
  Forwarding_unit forwarding_unit_1 (
    .regwriteex(ex_mem_1_regwrite_o), .regwritemem(mem_wb_1_regwrite_o), .pcra1(id_ex_1_ra1_o),
    .pcra2(id_ex_1_ra2_o), .pcradex(ex_mem_1_rw_o), .pcradmem(mem_wb_1_rw_o), .fora(forwarding_unit_1_fora),
    .forb(forwarding_unit_1_forb));
  EX_MEM ex_mem_1 (
    .clock(clock_1_out), .branch_res(somador_2_s), .alu_res(multiplexer_8_out), .rd2(id_ex_1_rd2_o),
    .rw(id_ex_1_rw_o), .regwrite(id_ex_1_regwrite_o), .memread(id_ex_1_memread_o),
    .memwrite(id_ex_1_memwrite_o), .memtoreg(id_ex_1_memtoreg_o), .zero(aluc_1_zero),
    .branch(id_ex_1_branch_o), .flush(hazard_unit_1_flush), .branch_res_o(ex_mem_1_branch_res_o),
    .alu_res_o(ex_mem_1_alu_res_o), .rd2_o(ex_mem_1_rd2_o), .rw_o(ex_mem_1_rw_o),
    .regwrite_o(ex_mem_1_regwrite_o), .memread_o(ex_mem_1_memread_o), .memwrite_o(ex_mem_1_memwrite_o),
    .memtoreg_o(ex_mem_1_memtoreg_o), .zero_o(ex_mem_1_zero_o), .branch_o(ex_mem_1_branch_o));
  RAM #(.addrWidth(24), .dataWidth(32), .trigger("high"), .\type ("nonvolatile")) data_mem (
    .addr(ex_mem_1_alu_res_o[23:0]), .we(ex_mem_1_memwrite_o), .oe(ex_mem_1_memread_o), .din(ex_mem_1_rd2_o),
    .dout(data_mem_dout));
  Branch_ctrl branch_ctrl_1 (.aluzero(ex_mem_1_zero_o), .branch(ex_mem_1_branch_o), .pcsrc(branch_ctrl_1_pcsrc));
  MEM_WB mem_wb_1 (
    .clock(clock_1_out), .rdm(data_mem_dout), .alu_res(ex_mem_1_alu_res_o), .regwrite(ex_mem_1_regwrite_o),
    .memtoreg(ex_mem_1_memtoreg_o), .rw(ex_mem_1_rw_o), .rdm_o(mem_wb_1_rdm_o),
    .alu_res_o(mem_wb_1_alu_res_o), .regwrite_o(mem_wb_1_regwrite_o), .memtoreg_o(mem_wb_1_memtoreg_o),
    .rw_o(mem_wb_1_rw_o));
  Multiplexer #(.width(32)) multiplexer_9 (
    .in0(mem_wb_1_alu_res_o), .in1(mem_wb_1_rdm_o), .out(multiplexer_9_out), .sel(mem_wb_1_memtoreg_o));

  // Notes on the sheet:
  //   contents of Instruction_mem (hex, n*v repeats v):
  //   202123 4*0 20056f 2583 350593 1111
endmodule

module ALUc (
  input  [31:0] a,
  input  [31:0] b,
  input  [1:0] Vec_size,
  input  [3:0] op,
  output zero,
  output [31:0] r
);

  wire alu_1_mode, alu_1_r_select;
  wire [31:0] alu_1_ae, alu_1_be, alu_1_r, carry_lookahead_1_s;

  ALU alu_1 (
    .a(a), .b(b), .op(op), .vec_size(Vec_size), .r_select(alu_1_r_select), .mode(alu_1_mode), .r(alu_1_r),
    .ae(alu_1_ae), .be(alu_1_be));
  CARRY_LOOKAHEAD carry_lookahead_1 (
    .A(alu_1_ae), .B(alu_1_be), .mode(alu_1_mode), .Vec_size(Vec_size), .S(carry_lookahead_1_s));
  Multiplexer #(.width(32)) multiplexer_1 (.in0(alu_1_r), .in1(carry_lookahead_1_s), .out(r), .sel(alu_1_r_select));
  zero_analyzer zero_analyzer_1 (.r(r), .zero(zero));
endmodule

// VHDL entity PC, as the project stores it:
--------------------------------------------------------------------------------
-- Project :
-- File    :
-- Autor   :
-- Date    :
--
--------------------------------------------------------------------------------
-- Description :
--
--------------------------------------------------------------------------------

LIBRARY ieee;
USE ieee.std_logic_1164.all;

ENTITY PC IS
  PORT (
  ------------------------------------------------------------------------------
  --Insert input ports below
    clock, reset,write_e      : IN  std_logic;
    a : IN std_logic_vector (31 DOWNTO 0);
    b : OUT std_logic_vector (31 DOWNTO 0)
    );
END PC;

--------------------------------------------------------------------------------
--Complete your VHDL description below
--------------------------------------------------------------------------------

ARCHITECTURE TypeArchitecture OF PC IS

BEGIN

PROCESS (clock, reset)
BEGIN
IF (write_e = '1') THEN
IF (rising_edge(clock)) THEN
	IF (a = "UUUUUUUUUUUUUUUUUUUUUUUUUUUUUUUU") THEN 
		 b <= "00000000000000000000000000000000";
	ELSE
		b <= a;
	END IF;
END IF;
IF (reset = '1') THEN
	 b <= "00000000000000000000000000000000";
END IF; 
END IF;
END PROCESS;

END TypeArchitecture;

// VHDL entity Somador, as the project stores it:
--------------------------------------------------------------------------------
-- Project :
-- File    :
-- Autor   :
-- Date    :
--
--------------------------------------------------------------------------------
-- Description :
--
--------------------------------------------------------------------------------

library IEEE;

use ieee.std_logic_1164.all;
use ieee.numeric_std.all;

 entity Somador is

  port(A, B_u : in std_logic_vector (31 downto 0);
  S : out std_logic_vector (31 downto 0));

 end Somador;

 architecture TypeArchitecture of Somador is
 signal C     : std_logic_vector (31 downto 0);
 signal control  : std_logic_vector (2 downto 0);
 signal mode : std_logic;
 begin
 
    control(0) <= '1';
    control(1) <= '1';
    control(2) <= '1';
    mode <= '0';
    
Carrys:process(C, control, mode, A, B_u)
begin
    C(0) <= mode;
    C(1) <= (A(0) and B_u(0)) or ((A(0) or B_u(0)) and (mode));
    C(2) <= (A(1) and B_u(1)) or ((A(1) or B_u(1)) and ((A(0) and B_u(0)) or ((A(0) or B_u(0)) and (mode))));
    C(3) <= (A(2) and B_u(2)) or ((A(2) or B_u(2)) and ((A(1) and B_u(1)) or ((A(1) or B_u(1)) and ((A(0) and B_u(0)) or ((A(0) or B_u(0)) and (mode))))));
    C(4) <= (((A(3) and B_u(3)) or ((A(3) or B_u(3)) and ((A(2) and B_u(2)) or ((A(2) or B_u(2)) and ((A(1) and B_u(1)) or ((A(1) or B_u(1)) and ((A(0) and B_u(0)) or ((A(0) or B_u(0)) and (mode))))))))) and control(0)) or (mode and (not control(0)));
    C(5) <= (A(4) and B_u(4)) or ((A(4) or B_u(4)) and ((((A(3) and B_u(3)) or ((A(3) or B_u(3)) and ((A(2) and B_u(2)) or ((A(2) or B_u(2)) and ((A(1) and B_u(1)) or ((A(1) or B_u(1)) and ((A(0) and B_u(0)) or ((A(0) or B_u(0)) and (mode))))))))) and control(0)) or (mode and (not control(0)))));
    C(6) <= (A(5) and B_u(5)) or ((A(5) or B_u(5)) and ((A(4) and B_u(4)) or ((A(4) or B_u(4)) and ((((A(3) and B_u(3)) or ((A(3) or B_u(3)) and ((A(2) and B_u(2)) or ((A(2) or B_u(2)) and ((A(1) and B_u(1)) or ((A(1) or B_u(1)) and ((A(0) and B_u(0)) or ((A(0) or B_u(0)) and (mode))))))))) and control(0)) or (mode and (not control(0)))))));
    C(7) <= (A(6) and B_u(6)) or ((A(6) or B_u(6)) and ((A(5) and B_u(5)) or ((A(5) or B_u(5)) and ((A(4) and B_u(4)) or ((A(4) or B_u(4)) and ((((A(3) and B_u(3)) or ((A(3) or B_u(3)) and ((A(2) and B_u(2)) or ((A(2) or B_u(2)) and ((A(1) and B_u(1)) or ((A(1) or B_u(1)) and ((A(0) and B_u(0)) or ((A(0) or B_u(0)) and (mode))))))))) and control(0)) or (mode and (not control(0)))))))));
    C(8) <= (((A(7) and B_u(7)) or ((A(7) or B_u(7)) and ((A(6) and B_u(6)) or ((A(6) or B_u(6)) and ((A(5) and B_u(5)) or ((A(5) or B_u(5)) and ((A(4) and B_u(4)) or ((A(4) or B_u(4)) and ((((A(3) and B_u(3)) or ((A(3) or B_u(3)) and ((A(2) and B_u(2)) or ((A(2) or B_u(2)) and ((A(1) and B_u(1)) or ((A(1) or B_u(1)) and ((A(0) and B_u(0)) or ((A(0) or B_u(0)) and (mode))))))))) and control(0)) or (mode and (not control(0)))))))))))) and control(1)) or (mode and (not control(1)));
    C(9) <= (A(8) and B_u(8)) or ((A(8) or B_u(8)) and ((((A(7) and B_u(7)) or ((A(7) or B_u(7)) and ((A(6) and B_u(6)) or ((A(6) or B_u(6)) and ((A(5) and B_u(5)) or ((A(5) or B_u(5)) and ((A(4) and B_u(4)) or ((A(4) or B_u(4)) and ((((A(3) and B_u(3)) or ((A(3) or B_u(3)) and ((A(2) and B_u(2)) or ((A(2) or B_u(2)) and ((A(1) and B_u(1)) or ((A(1) or B_u(1)) and ((A(0) and B_u(0)) or ((A(0) or B_u(0)) and (mode))))))))) and control(0)) or (mode and (not control(0)))))))))))) and control(1)) or (mode and (not control(1)))));
    C(10) <= (A(9) and B_u(9)) or ((A(9) or B_u(9)) and ((A(8) and B_u(8)) or ((A(8) or B_u(8)) and ((((A(7) and B_u(7)) or ((A(7) or B_u(7)) and ((A(6) and B_u(6)) or ((A(6) or B_u(6)) and ((A(5) and B_u(5)) or ((A(5) or B_u(5)) and ((A(4) and B_u(4)) or ((A(4) or B_u(4)) and ((((A(3) and B_u(3)) or ((A(3) or B_u(3)) and ((A(2) and B_u(2)) or ((A(2) or B_u(2)) and ((A(1) and B_u(1)) or ((A(1) or B_u(1)) and ((A(0) and B_u(0)) or ((A(0) or B_u(0)) and (mode))))))))) and control(0)) or (mode and (not control(0)))))))))))) and control(1)) or (mode and (not control(1)))))));
    C(11) <= (A(10) and B_u(10)) or ((A(10) or B_u(10)) and ((A(9) and B_u(9)) or ((A(9) or B_u(9)) and ((A(8) and B_u(8)) or ((A(8) or B_u(8)) and ((((A(7) and B_u(7)) or ((A(7) or B_u(7)) and ((A(6) and B_u(6)) or ((A(6) or B_u(6)) and ((A(5) and B_u(5)) or ((A(5) or B_u(5)) and ((A(4) and B_u(4)) or ((A(4) or B_u(4)) and ((((A(3) and B_u(3)) or ((A(3) or B_u(3)) and ((A(2) and B_u(2)) or ((A(2) or B_u(2)) and ((A(1) and B_u(1)) or ((A(1) or B_u(1)) and ((A(0) and B_u(0)) or ((A(0) or B_u(0)) and (mode))))))))) and control(0)) or (mode and (not control(0)))))))))))) and control(1)) or (mode and (not control(1)))))))));
    C(12) <= (((A(11) and B_u(11)) or ((A(11) or B_u(11)) and ((A(10) and B_u(10)) or ((A(10) or B_u(10)) and ((A(9) and B_u(9)) or ((A(9) or B_u(9)) and ((A(8) and B_u(8)) or ((A(8) or B_u(8)) and ((((A(7) and B_u(7)) or ((A(7) or B_u(7)) and ((A(6) and B_u(6)) or ((A(6) or B_u(6)) and ((A(5) and B_u(5)) or ((A(5) or B_u(5)) and ((A(4) and B_u(4)) or ((A(4) or B_u(4)) and ((((A(3) and B_u(3)) or ((A(3) or B_u(3)) and ((A(2) and B_u(2)) or ((A(2) or B_u(2)) and ((A(1) and B_u(1)) or ((A(1) or B_u(1)) and ((A(0) and B_u(0)) or ((A(0) or B_u(0)) and (mode))))))))) and control(0)) or (mode and (not control(0)))))))))))) and control(1)) or (mode and (not control(1)))))))))))) and control(0)) or (mode and (not control(0)));
    C(13) <= (A(12) and B_u(12)) or ((A(12) or B_u(12)) and ((((A(11) and B_u(11)) or ((A(11) or B_u(11)) and ((A(10) and B_u(10)) or ((A(10) or B_u(10)) and ((A(9) and B_u(9)) or ((A(9) or B_u(9)) and ((A(8) and B_u(8)) or ((A(8) or B_u(8)) and ((((A(7) and B_u(7)) or ((A(7) or B_u(7)) and ((A(6) and B_u(6)) or ((A(6) or B_u(6)) and ((A(5) and B_u(5)) or ((A(5) or B_u(5)) and ((A(4) and B_u(4)) or ((A(4) or B_u(4)) and ((((A(3) and B_u(3)) or ((A(3) or B_u(3)) and ((A(2) and B_u(2)) or ((A(2) or B_u(2)) and ((A(1) and B_u(1)) or ((A(1) or B_u(1)) and ((A(0) and B_u(0)) or ((A(0) or B_u(0)) and (mode))))))))) and control(0)) or (mode and (not control(0)))))))))))) and control(1)) or (mode and (not control(1)))))))))))) and control(0)) or (mode and (not control(0)))));
    C(14) <= (A(13) and B_u(13)) or ((A(13) or B_u(13)) and ((A(12) and B_u(12)) or ((A(12) or B_u(12)) and ((((A(11) and B_u(11)) or ((A(11) or B_u(11)) and ((A(10) and B_u(10)) or ((A(10) or B_u(10)) and ((A(9) and B_u(9)) or ((A(9) or B_u(9)) and ((A(8) and B_u(8)) or ((A(8) or B_u(8)) and ((((A(7) and B_u(7)) or ((A(7) or B_u(7)) and ((A(6) and B_u(6)) or ((A(6) or B_u(6)) and ((A(5) and B_u(5)) or ((A(5) or B_u(5)) and ((A(4) and B_u(4)) or ((A(4) or B_u(4)) and ((((A(3) and B_u(3)) or ((A(3) or B_u(3)) and ((A(2) and B_u(2)) or ((A(2) or B_u(2)) and ((A(1) and B_u(1)) or ((A(1) or B_u(1)) and ((A(0) and B_u(0)) or ((A(0) or B_u(0)) and (mode))))))))) and control(0)) or (mode and (not control(0)))))))))))) and control(1)) or (mode and (not control(1)))))))))))) and control(0)) or (mode and (not control(0)))))));
    C(15) <= (A(14) and B_u(14)) or ((A(14) or B_u(14)) and ((A(13) and B_u(13)) or ((A(13) or B_u(13)) and ((A(12) and B_u(12)) or ((A(12) or B_u(12)) and ((((A(11) and B_u(11)) or ((A(11) or B_u(11)) and ((A(10) and B_u(10)) or ((A(10) or B_u(10)) and ((A(9) and B_u(9)) or ((A(9) or B_u(9)) and ((A(8) and B_u(8)) or ((A(8) or B_u(8)) and ((((A(7) and B_u(7)) or ((A(7) or B_u(7)) and ((A(6) and B_u(6)) or ((A(6) or B_u(6)) and ((A(5) and B_u(5)) or ((A(5) or B_u(5)) and ((A(4) and B_u(4)) or ((A(4) or B_u(4)) and ((((A(3) and B_u(3)) or ((A(3) or B_u(3)) and ((A(2) and B_u(2)) or ((A(2) or B_u(2)) and ((A(1) and B_u(1)) or ((A(1) or B_u(1)) and ((A(0) and B_u(0)) or ((A(0) or B_u(0)) and (mode))))))))) and control(0)) or (mode and (not control(0)))))))))))) and control(1)) or (mode and (not control(1)))))))))))) and control(0)) or (mode and (not control(0)))))))));
    C(16) <= (((A(15) and B_u(15)) or ((A(15) or B_u(15)) and ((A(14) and B_u(14)) or ((A(14) or B_u(14)) and ((A(13) and B_u(13)) or ((A(13) or B_u(13)) and ((A(12) and B_u(12)) or ((A(12) or B_u(12)) and ((((A(11) and B_u(11)) or ((A(11) or B_u(11)) and ((A(10) and B_u(10)) or ((A(10) or B_u(10)) and ((A(9) and B_u(9)) or ((A(9) or B_u(9)) and ((A(8) and B_u(8)) or ((A(8) or B_u(8)) and ((((A(7) and B_u(7)) or ((A(7) or B_u(7)) and ((A(6) and B_u(6)) or ((A(6) or B_u(6)) and ((A(5) and B_u(5)) or ((A(5) or B_u(5)) and ((A(4) and B_u(4)) or ((A(4) or B_u(4)) and ((((A(3) and B_u(3)) or ((A(3) or B_u(3)) and ((A(2) and B_u(2)) or ((A(2) or B_u(2)) and ((A(1) and B_u(1)) or ((A(1) or B_u(1)) and ((A(0) and B_u(0)) or ((A(0) or B_u(0)) and (mode))))))))) and control(0)) or (mode and (not control(0)))))))))))) and control(1)) or (mode and (not control(1)))))))))))) and control(0)) or (mode and (not control(0)))))))))))) and control(2)) or (mode and (not control(2)));
    C(17) <= (A(16) and B_u(16)) or ((A(16) or B_u(16)) and ((((A(15) and B_u(15)) or ((A(15) or B_u(15)) and ((A(14) and B_u(14)) or ((A(14) or B_u(14)) and ((A(13) and B_u(13)) or ((A(13) or B_u(13)) and ((A(12) and B_u(12)) or ((A(12) or B_u(12)) and ((((A(11) and B_u(11)) or ((A(11) or B_u(11)) and ((A(10) and B_u(10)) or ((A(10) or B_u(10)) and ((A(9) and B_u(9)) or ((A(9) or B_u(9)) and ((A(8) and B_u(8)) or ((A(8) or B_u(8)) and ((((A(7) and B_u(7)) or ((A(7) or B_u(7)) and ((A(6) and B_u(6)) or ((A(6) or B_u(6)) and ((A(5) and B_u(5)) or ((A(5) or B_u(5)) and ((A(4) and B_u(4)) or ((A(4) or B_u(4)) and ((((A(3) and B_u(3)) or ((A(3) or B_u(3)) and ((A(2) and B_u(2)) or ((A(2) or B_u(2)) and ((A(1) and B_u(1)) or ((A(1) or B_u(1)) and ((A(0) and B_u(0)) or ((A(0) or B_u(0)) and (mode))))))))) and control(0)) or (mode and (not control(0)))))))))))) and control(1)) or (mode and (not control(1)))))))))))) and control(0)) or (mode and (not control(0)))))))))))) and control(2)) or (mode and (not control(2)))));
    C(18) <= (A(17) and B_u(17)) or ((A(17) or B_u(17)) and ((A(16) and B_u(16)) or ((A(16) or B_u(16)) and ((((A(15) and B_u(15)) or ((A(15) or B_u(15)) and ((A(14) and B_u(14)) or ((A(14) or B_u(14)) and ((A(13) and B_u(13)) or ((A(13) or B_u(13)) and ((A(12) and B_u(12)) or ((A(12) or B_u(12)) and ((((A(11) and B_u(11)) or ((A(11) or B_u(11)) and ((A(10) and B_u(10)) or ((A(10) or B_u(10)) and ((A(9) and B_u(9)) or ((A(9) or B_u(9)) and ((A(8) and B_u(8)) or ((A(8) or B_u(8)) and ((((A(7) and B_u(7)) or ((A(7) or B_u(7)) and ((A(6) and B_u(6)) or ((A(6) or B_u(6)) and ((A(5) and B_u(5)) or ((A(5) or B_u(5)) and ((A(4) and B_u(4)) or ((A(4) or B_u(4)) and ((((A(3) and B_u(3)) or ((A(3) or B_u(3)) and ((A(2) and B_u(2)) or ((A(2) or B_u(2)) and ((A(1) and B_u(1)) or ((A(1) or B_u(1)) and ((A(0) and B_u(0)) or ((A(0) or B_u(0)) and (mode))))))))) and control(0)) or (mode and (not control(0)))))))))))) and control(1)) or (mode and (not control(1)))))))))))) and control(0)) or (mode and (not control(0)))))))))))) and control(2)) or (mode and (not control(2)))))));
    C(19) <= (A(18) and B_u(18)) or ((A(18) or B_u(18)) and ((A(17) and B_u(17)) or ((A(17) or B_u(17)) and ((A(16) and B_u(16)) or ((A(16) or B_u(16)) and ((((A(15) and B_u(15)) or ((A(15) or B_u(15)) and ((A(14) and B_u(14)) or ((A(14) or B_u(14)) and ((A(13) and B_u(13)) or ((A(13) or B_u(13)) and ((A(12) and B_u(12)) or ((A(12) or B_u(12)) and ((((A(11) and B_u(11)) or ((A(11) or B_u(11)) and ((A(10) and B_u(10)) or ((A(10) or B_u(10)) and ((A(9) and B_u(9)) or ((A(9) or B_u(9)) and ((A(8) and B_u(8)) or ((A(8) or B_u(8)) and ((((A(7) and B_u(7)) or ((A(7) or B_u(7)) and ((A(6) and B_u(6)) or ((A(6) or B_u(6)) and ((A(5) and B_u(5)) or ((A(5) or B_u(5)) and ((A(4) and B_u(4)) or ((A(4) or B_u(4)) and ((((A(3) and B_u(3)) or ((A(3) or B_u(3)) and ((A(2) and B_u(2)) or ((A(2) or B_u(2)) and ((A(1) and B_u(1)) or ((A(1) or B_u(1)) and ((A(0) and B_u(0)) or ((A(0) or B_u(0)) and (mode))))))))) and control(0)) or (mode and (not control(0)))))))))))) and control(1)) or (mode and (not control(1)))))))))))) and control(0)) or (mode and (not control(0)))))))))))) and control(2)) or (mode and (not control(2)))))))));
    C(20) <= (((A(19) and B_u(19)) or ((A(19) or B_u(19)) and ((A(18) and B_u(18)) or ((A(18) or B_u(18)) and ((A(17) and B_u(17)) or ((A(17) or B_u(17)) and ((A(16) and B_u(16)) or ((A(16) or B_u(16)) and ((((A(15) and B_u(15)) or ((A(15) or B_u(15)) and ((A(14) and B_u(14)) or ((A(14) or B_u(14)) and ((A(13) and B_u(13)) or ((A(13) or B_u(13)) and ((A(12) and B_u(12)) or ((A(12) or B_u(12)) and ((((A(11) and B_u(11)) or ((A(11) or B_u(11)) and ((A(10) and B_u(10)) or ((A(10) or B_u(10)) and ((A(9) and B_u(9)) or ((A(9) or B_u(9)) and ((A(8) and B_u(8)) or ((A(8) or B_u(8)) and ((((A(7) and B_u(7)) or ((A(7) or B_u(7)) and ((A(6) and B_u(6)) or ((A(6) or B_u(6)) and ((A(5) and B_u(5)) or ((A(5) or B_u(5)) and ((A(4) and B_u(4)) or ((A(4) or B_u(4)) and ((((A(3) and B_u(3)) or ((A(3) or B_u(3)) and ((A(2) and B_u(2)) or ((A(2) or B_u(2)) and ((A(1) and B_u(1)) or ((A(1) or B_u(1)) and ((A(0) and B_u(0)) or ((A(0) or B_u(0)) and (mode))))))))) and control(0)) or (mode and (not control(0)))))))))))) and control(1)) or (mode and (not control(1)))))))))))) and control(0)) or (mode and (not control(0)))))))))))) and control(2)) or (mode and (not control(2)))))))))))) and control(0)) or (mode and (not control(0)));
    C(21) <= (A(20) and B_u(20)) or ((A(20) or B_u(20)) and ((((A(19) and B_u(19)) or ((A(19) or B_u(19)) and ((A(18) and B_u(18)) or ((A(18) or B_u(18)) and ((A(17) and B_u(17)) or ((A(17) or B_u(17)) and ((A(16) and B_u(16)) or ((A(16) or B_u(16)) and ((((A(15) and B_u(15)) or ((A(15) or B_u(15)) and ((A(14) and B_u(14)) or ((A(14) or B_u(14)) and ((A(13) and B_u(13)) or ((A(13) or B_u(13)) and ((A(12) and B_u(12)) or ((A(12) or B_u(12)) and ((((A(11) and B_u(11)) or ((A(11) or B_u(11)) and ((A(10) and B_u(10)) or ((A(10) or B_u(10)) and ((A(9) and B_u(9)) or ((A(9) or B_u(9)) and ((A(8) and B_u(8)) or ((A(8) or B_u(8)) and ((((A(7) and B_u(7)) or ((A(7) or B_u(7)) and ((A(6) and B_u(6)) or ((A(6) or B_u(6)) and ((A(5) and B_u(5)) or ((A(5) or B_u(5)) and ((A(4) and B_u(4)) or ((A(4) or B_u(4)) and ((((A(3) and B_u(3)) or ((A(3) or B_u(3)) and ((A(2) and B_u(2)) or ((A(2) or B_u(2)) and ((A(1) and B_u(1)) or ((A(1) or B_u(1)) and ((A(0) and B_u(0)) or ((A(0) or B_u(0)) and (mode))))))))) and control(0)) or (mode and (not control(0)))))))))))) and control(1)) or (mode and (not control(1)))))))))))) and control(0)) or (mode and (not control(0)))))))))))) and control(2)) or (mode and (not control(2)))))))))))) and control(0)) or (mode and (not control(0)))));
    C(22) <= (A(21) and B_u(21)) or ((A(21) or B_u(21)) and ((A(20) and B_u(20)) or ((A(20) or B_u(20)) and ((((A(19) and B_u(19)) or ((A(19) or B_u(19)) and ((A(18) and B_u(18)) or ((A(18) or B_u(18)) and ((A(17) and B_u(17)) or ((A(17) or B_u(17)) and ((A(16) and B_u(16)) or ((A(16) or B_u(16)) and ((((A(15) and B_u(15)) or ((A(15) or B_u(15)) and ((A(14) and B_u(14)) or ((A(14) or B_u(14)) and ((A(13) and B_u(13)) or ((A(13) or B_u(13)) and ((A(12) and B_u(12)) or ((A(12) or B_u(12)) and ((((A(11) and B_u(11)) or ((A(11) or B_u(11)) and ((A(10) and B_u(10)) or ((A(10) or B_u(10)) and ((A(9) and B_u(9)) or ((A(9) or B_u(9)) and ((A(8) and B_u(8)) or ((A(8) or B_u(8)) and ((((A(7) and B_u(7)) or ((A(7) or B_u(7)) and ((A(6) and B_u(6)) or ((A(6) or B_u(6)) and ((A(5) and B_u(5)) or ((A(5) or B_u(5)) and ((A(4) and B_u(4)) or ((A(4) or B_u(4)) and ((((A(3) and B_u(3)) or ((A(3) or B_u(3)) and ((A(2) and B_u(2)) or ((A(2) or B_u(2)) and ((A(1) and B_u(1)) or ((A(1) or B_u(1)) and ((A(0) and B_u(0)) or ((A(0) or B_u(0)) and (mode))))))))) and control(0)) or (mode and (not control(0)))))))))))) and control(1)) or (mode and (not control(1)))))))))))) and control(0)) or (mode and (not control(0)))))))))))) and control(2)) or (mode and (not control(2)))))))))))) and control(0)) or (mode and (not control(0)))))));
    C(23) <= (A(22) and B_u(22)) or ((A(22) or B_u(22)) and ((A(21) and B_u(21)) or ((A(21) or B_u(21)) and ((A(20) and B_u(20)) or ((A(20) or B_u(20)) and ((((A(19) and B_u(19)) or ((A(19) or B_u(19)) and ((A(18) and B_u(18)) or ((A(18) or B_u(18)) and ((A(17) and B_u(17)) or ((A(17) or B_u(17)) and ((A(16) and B_u(16)) or ((A(16) or B_u(16)) and ((((A(15) and B_u(15)) or ((A(15) or B_u(15)) and ((A(14) and B_u(14)) or ((A(14) or B_u(14)) and ((A(13) and B_u(13)) or ((A(13) or B_u(13)) and ((A(12) and B_u(12)) or ((A(12) or B_u(12)) and ((((A(11) and B_u(11)) or ((A(11) or B_u(11)) and ((A(10) and B_u(10)) or ((A(10) or B_u(10)) and ((A(9) and B_u(9)) or ((A(9) or B_u(9)) and ((A(8) and B_u(8)) or ((A(8) or B_u(8)) and ((((A(7) and B_u(7)) or ((A(7) or B_u(7)) and ((A(6) and B_u(6)) or ((A(6) or B_u(6)) and ((A(5) and B_u(5)) or ((A(5) or B_u(5)) and ((A(4) and B_u(4)) or ((A(4) or B_u(4)) and ((((A(3) and B_u(3)) or ((A(3) or B_u(3)) and ((A(2) and B_u(2)) or ((A(2) or B_u(2)) and ((A(1) and B_u(1)) or ((A(1) or B_u(1)) and ((A(0) and B_u(0)) or ((A(0) or B_u(0)) and (mode))))))))) and control(0)) or (mode and (not control(0)))))))))))) and control(1)) or (mode and (not control(1)))))))))))) and control(0)) or (mode and (not control(0)))))))))))) and control(2)) or (mode and (not control(2)))))))))))) and control(0)) or (mode and (not control(0)))))))));
    C(24) <= (((A(23) and B_u(23)) or ((A(23) or B_u(23)) and ((A(22) and B_u(22)) or ((A(22) or B_u(22)) and ((A(21) and B_u(21)) or ((A(21) or B_u(21)) and ((A(20) and B_u(20)) or ((A(20) or B_u(20)) and ((((A(19) and B_u(19)) or ((A(19) or B_u(19)) and ((A(18) and B_u(18)) or ((A(18) or B_u(18)) and ((A(17) and B_u(17)) or ((A(17) or B_u(17)) and ((A(16) and B_u(16)) or ((A(16) or B_u(16)) and ((((A(15) and B_u(15)) or ((A(15) or B_u(15)) and ((A(14) and B_u(14)) or ((A(14) or B_u(14)) and ((A(13) and B_u(13)) or ((A(13) or B_u(13)) and ((A(12) and B_u(12)) or ((A(12) or B_u(12)) and ((((A(11) and B_u(11)) or ((A(11) or B_u(11)) and ((A(10) and B_u(10)) or ((A(10) or B_u(10)) and ((A(9) and B_u(9)) or ((A(9) or B_u(9)) and ((A(8) and B_u(8)) or ((A(8) or B_u(8)) and ((((A(7) and B_u(7)) or ((A(7) or B_u(7)) and ((A(6) and B_u(6)) or ((A(6) or B_u(6)) and ((A(5) and B_u(5)) or ((A(5) or B_u(5)) and ((A(4) and B_u(4)) or ((A(4) or B_u(4)) and ((((A(3) and B_u(3)) or ((A(3) or B_u(3)) and ((A(2) and B_u(2)) or ((A(2) or B_u(2)) and ((A(1) and B_u(1)) or ((A(1) or B_u(1)) and ((A(0) and B_u(0)) or ((A(0) or B_u(0)) and (mode))))))))) and control(0)) or (mode and (not control(0)))))))))))) and control(1)) or (mode and (not control(1)))))))))))) and control(0)) or (mode and (not control(0)))))))))))) and control(2)) or (mode and (not control(2)))))))))))) and control(0)) or (mode and (not control(0)))))))))))) and control(1)) or (mode and (not control(1)));
    C(25) <= (A(24) and B_u(24)) or ((A(24) or B_u(24)) and ((((A(23) and B_u(23)) or ((A(23) or B_u(23)) and ((A(22) and B_u(22)) or ((A(22) or B_u(22)) and ((A(21) and B_u(21)) or ((A(21) or B_u(21)) and ((A(20) and B_u(20)) or ((A(20) or B_u(20)) and ((((A(19) and B_u(19)) or ((A(19) or B_u(19)) and ((A(18) and B_u(18)) or ((A(18) or B_u(18)) and ((A(17) and B_u(17)) or ((A(17) or B_u(17)) and ((A(16) and B_u(16)) or ((A(16) or B_u(16)) and ((((A(15) and B_u(15)) or ((A(15) or B_u(15)) and ((A(14) and B_u(14)) or ((A(14) or B_u(14)) and ((A(13) and B_u(13)) or ((A(13) or B_u(13)) and ((A(12) and B_u(12)) or ((A(12) or B_u(12)) and ((((A(11) and B_u(11)) or ((A(11) or B_u(11)) and ((A(10) and B_u(10)) or ((A(10) or B_u(10)) and ((A(9) and B_u(9)) or ((A(9) or B_u(9)) and ((A(8) and B_u(8)) or ((A(8) or B_u(8)) and ((((A(7) and B_u(7)) or ((A(7) or B_u(7)) and ((A(6) and B_u(6)) or ((A(6) or B_u(6)) and ((A(5) and B_u(5)) or ((A(5) or B_u(5)) and ((A(4) and B_u(4)) or ((A(4) or B_u(4)) and ((((A(3) and B_u(3)) or ((A(3) or B_u(3)) and ((A(2) and B_u(2)) or ((A(2) or B_u(2)) and ((A(1) and B_u(1)) or ((A(1) or B_u(1)) and ((A(0) and B_u(0)) or ((A(0) or B_u(0)) and (mode))))))))) and control(0)) or (mode and (not control(0)))))))))))) and control(1)) or (mode and (not control(1)))))))))))) and control(0)) or (mode and (not control(0)))))))))))) and control(2)) or (mode and (not control(2)))))))))))) and control(0)) or (mode and (not control(0)))))))))))) and control(1)) or (mode and (not control(1)))));
    C(26) <= (A(25) and B_u(25)) or ((A(25) or B_u(25)) and ((A(24) and B_u(24)) or ((A(24) or B_u(24)) and ((((A(23) and B_u(23)) or ((A(23) or B_u(23)) and ((A(22) and B_u(22)) or ((A(22) or B_u(22)) and ((A(21) and B_u(21)) or ((A(21) or B_u(21)) and ((A(20) and B_u(20)) or ((A(20) or B_u(20)) and ((((A(19) and B_u(19)) or ((A(19) or B_u(19)) and ((A(18) and B_u(18)) or ((A(18) or B_u(18)) and ((A(17) and B_u(17)) or ((A(17) or B_u(17)) and ((A(16) and B_u(16)) or ((A(16) or B_u(16)) and ((((A(15) and B_u(15)) or ((A(15) or B_u(15)) and ((A(14) and B_u(14)) or ((A(14) or B_u(14)) and ((A(13) and B_u(13)) or ((A(13) or B_u(13)) and ((A(12) and B_u(12)) or ((A(12) or B_u(12)) and ((((A(11) and B_u(11)) or ((A(11) or B_u(11)) and ((A(10) and B_u(10)) or ((A(10) or B_u(10)) and ((A(9) and B_u(9)) or ((A(9) or B_u(9)) and ((A(8) and B_u(8)) or ((A(8) or B_u(8)) and ((((A(7) and B_u(7)) or ((A(7) or B_u(7)) and ((A(6) and B_u(6)) or ((A(6) or B_u(6)) and ((A(5) and B_u(5)) or ((A(5) or B_u(5)) and ((A(4) and B_u(4)) or ((A(4) or B_u(4)) and ((((A(3) and B_u(3)) or ((A(3) or B_u(3)) and ((A(2) and B_u(2)) or ((A(2) or B_u(2)) and ((A(1) and B_u(1)) or ((A(1) or B_u(1)) and ((A(0) and B_u(0)) or ((A(0) or B_u(0)) and (mode))))))))) and control(0)) or (mode and (not control(0)))))))))))) and control(1)) or (mode and (not control(1)))))))))))) and control(0)) or (mode and (not control(0)))))))))))) and control(2)) or (mode and (not control(2)))))))))))) and control(0)) or (mode and (not control(0)))))))))))) and control(1)) or (mode and (not control(1)))))));
    C(27) <= (A(26) and B_u(26)) or ((A(26) or B_u(26)) and ((A(25) and B_u(25)) or ((A(25) or B_u(25)) and ((A(24) and B_u(24)) or ((A(24) or B_u(24)) and ((((A(23) and B_u(23)) or ((A(23) or B_u(23)) and ((A(22) and B_u(22)) or ((A(22) or B_u(22)) and ((A(21) and B_u(21)) or ((A(21) or B_u(21)) and ((A(20) and B_u(20)) or ((A(20) or B_u(20)) and ((((A(19) and B_u(19)) or ((A(19) or B_u(19)) and ((A(18) and B_u(18)) or ((A(18) or B_u(18)) and ((A(17) and B_u(17)) or ((A(17) or B_u(17)) and ((A(16) and B_u(16)) or ((A(16) or B_u(16)) and ((((A(15) and B_u(15)) or ((A(15) or B_u(15)) and ((A(14) and B_u(14)) or ((A(14) or B_u(14)) and ((A(13) and B_u(13)) or ((A(13) or B_u(13)) and ((A(12) and B_u(12)) or ((A(12) or B_u(12)) and ((((A(11) and B_u(11)) or ((A(11) or B_u(11)) and ((A(10) and B_u(10)) or ((A(10) or B_u(10)) and ((A(9) and B_u(9)) or ((A(9) or B_u(9)) and ((A(8) and B_u(8)) or ((A(8) or B_u(8)) and ((((A(7) and B_u(7)) or ((A(7) or B_u(7)) and ((A(6) and B_u(6)) or ((A(6) or B_u(6)) and ((A(5) and B_u(5)) or ((A(5) or B_u(5)) and ((A(4) and B_u(4)) or ((A(4) or B_u(4)) and ((((A(3) and B_u(3)) or ((A(3) or B_u(3)) and ((A(2) and B_u(2)) or ((A(2) or B_u(2)) and ((A(1) and B_u(1)) or ((A(1) or B_u(1)) and ((A(0) and B_u(0)) or ((A(0) or B_u(0)) and (mode))))))))) and control(0)) or (mode and (not control(0)))))))))))) and control(1)) or (mode and (not control(1)))))))))))) and control(0)) or (mode and (not control(0)))))))))))) and control(2)) or (mode and (not control(2)))))))))))) and control(0)) or (mode and (not control(0)))))))))))) and control(1)) or (mode and (not control(1)))))))));
    C(28) <= (((A(27) and B_u(27)) or ((A(27) or B_u(27)) and ((A(26) and B_u(26)) or ((A(26) or B_u(26)) and ((A(25) and B_u(25)) or ((A(25) or B_u(25)) and ((A(24) and B_u(24)) or ((A(24) or B_u(24)) and ((((A(23) and B_u(23)) or ((A(23) or B_u(23)) and ((A(22) and B_u(22)) or ((A(22) or B_u(22)) and ((A(21) and B_u(21)) or ((A(21) or B_u(21)) and ((A(20) and B_u(20)) or ((A(20) or B_u(20)) and ((((A(19) and B_u(19)) or ((A(19) or B_u(19)) and ((A(18) and B_u(18)) or ((A(18) or B_u(18)) and ((A(17) and B_u(17)) or ((A(17) or B_u(17)) and ((A(16) and B_u(16)) or ((A(16) or B_u(16)) and ((((A(15) and B_u(15)) or ((A(15) or B_u(15)) and ((A(14) and B_u(14)) or ((A(14) or B_u(14)) and ((A(13) and B_u(13)) or ((A(13) or B_u(13)) and ((A(12) and B_u(12)) or ((A(12) or B_u(12)) and ((((A(11) and B_u(11)) or ((A(11) or B_u(11)) and ((A(10) and B_u(10)) or ((A(10) or B_u(10)) and ((A(9) and B_u(9)) or ((A(9) or B_u(9)) and ((A(8) and B_u(8)) or ((A(8) or B_u(8)) and ((((A(7) and B_u(7)) or ((A(7) or B_u(7)) and ((A(6) and B_u(6)) or ((A(6) or B_u(6)) and ((A(5) and B_u(5)) or ((A(5) or B_u(5)) and ((A(4) and B_u(4)) or ((A(4) or B_u(4)) and ((((A(3) and B_u(3)) or ((A(3) or B_u(3)) and ((A(2) and B_u(2)) or ((A(2) or B_u(2)) and ((A(1) and B_u(1)) or ((A(1) or B_u(1)) and ((A(0) and B_u(0)) or ((A(0) or B_u(0)) and (mode))))))))) and control(0)) or (mode and (not control(0)))))))))))) and control(1)) or (mode and (not control(1)))))))))))) and control(0)) or (mode and (not control(0)))))))))))) and control(2)) or (mode and (not control(2)))))))))))) and control(0)) or (mode and (not control(0)))))))))))) and control(1)) or (mode and (not control(1)))))))))))) and control(0)) or (mode and (not control(0)));
    C(29) <= (A(28) and B_u(28)) or ((A(28) or B_u(28)) and ((((A(27) and B_u(27)) or ((A(27) or B_u(27)) and ((A(26) and B_u(26)) or ((A(26) or B_u(26)) and ((A(25) and B_u(25)) or ((A(25) or B_u(25)) and ((A(24) and B_u(24)) or ((A(24) or B_u(24)) and ((((A(23) and B_u(23)) or ((A(23) or B_u(23)) and ((A(22) and B_u(22)) or ((A(22) or B_u(22)) and ((A(21) and B_u(21)) or ((A(21) or B_u(21)) and ((A(20) and B_u(20)) or ((A(20) or B_u(20)) and ((((A(19) and B_u(19)) or ((A(19) or B_u(19)) and ((A(18) and B_u(18)) or ((A(18) or B_u(18)) and ((A(17) and B_u(17)) or ((A(17) or B_u(17)) and ((A(16) and B_u(16)) or ((A(16) or B_u(16)) and ((((A(15) and B_u(15)) or ((A(15) or B_u(15)) and ((A(14) and B_u(14)) or ((A(14) or B_u(14)) and ((A(13) and B_u(13)) or ((A(13) or B_u(13)) and ((A(12) and B_u(12)) or ((A(12) or B_u(12)) and ((((A(11) and B_u(11)) or ((A(11) or B_u(11)) and ((A(10) and B_u(10)) or ((A(10) or B_u(10)) and ((A(9) and B_u(9)) or ((A(9) or B_u(9)) and ((A(8) and B_u(8)) or ((A(8) or B_u(8)) and ((((A(7) and B_u(7)) or ((A(7) or B_u(7)) and ((A(6) and B_u(6)) or ((A(6) or B_u(6)) and ((A(5) and B_u(5)) or ((A(5) or B_u(5)) and ((A(4) and B_u(4)) or ((A(4) or B_u(4)) and ((((A(3) and B_u(3)) or ((A(3) or B_u(3)) and ((A(2) and B_u(2)) or ((A(2) or B_u(2)) and ((A(1) and B_u(1)) or ((A(1) or B_u(1)) and ((A(0) and B_u(0)) or ((A(0) or B_u(0)) and (mode))))))))) and control(0)) or (mode and (not control(0)))))))))))) and control(1)) or (mode and (not control(1)))))))))))) and control(0)) or (mode and (not control(0)))))))))))) and control(2)) or (mode and (not control(2)))))))))))) and control(0)) or (mode and (not control(0)))))))))))) and control(1)) or (mode and (not control(1)))))))))))) and control(0)) or (mode and (not control(0)))));
    C(30) <= (A(29) and B_u(29)) or ((A(29) or B_u(29)) and ((A(28) and B_u(28)) or ((A(28) or B_u(28)) and ((((A(27) and B_u(27)) or ((A(27) or B_u(27)) and ((A(26) and B_u(26)) or ((A(26) or B_u(26)) and ((A(25) and B_u(25)) or ((A(25) or B_u(25)) and ((A(24) and B_u(24)) or ((A(24) or B_u(24)) and ((((A(23) and B_u(23)) or ((A(23) or B_u(23)) and ((A(22) and B_u(22)) or ((A(22) or B_u(22)) and ((A(21) and B_u(21)) or ((A(21) or B_u(21)) and ((A(20) and B_u(20)) or ((A(20) or B_u(20)) and ((((A(19) and B_u(19)) or ((A(19) or B_u(19)) and ((A(18) and B_u(18)) or ((A(18) or B_u(18)) and ((A(17) and B_u(17)) or ((A(17) or B_u(17)) and ((A(16) and B_u(16)) or ((A(16) or B_u(16)) and ((((A(15) and B_u(15)) or ((A(15) or B_u(15)) and ((A(14) and B_u(14)) or ((A(14) or B_u(14)) and ((A(13) and B_u(13)) or ((A(13) or B_u(13)) and ((A(12) and B_u(12)) or ((A(12) or B_u(12)) and ((((A(11) and B_u(11)) or ((A(11) or B_u(11)) and ((A(10) and B_u(10)) or ((A(10) or B_u(10)) and ((A(9) and B_u(9)) or ((A(9) or B_u(9)) and ((A(8) and B_u(8)) or ((A(8) or B_u(8)) and ((((A(7) and B_u(7)) or ((A(7) or B_u(7)) and ((A(6) and B_u(6)) or ((A(6) or B_u(6)) and ((A(5) and B_u(5)) or ((A(5) or B_u(5)) and ((A(4) and B_u(4)) or ((A(4) or B_u(4)) and ((((A(3) and B_u(3)) or ((A(3) or B_u(3)) and ((A(2) and B_u(2)) or ((A(2) or B_u(2)) and ((A(1) and B_u(1)) or ((A(1) or B_u(1)) and ((A(0) and B_u(0)) or ((A(0) or B_u(0)) and (mode))))))))) and control(0)) or (mode and (not control(0)))))))))))) and control(1)) or (mode and (not control(1)))))))))))) and control(0)) or (mode and (not control(0)))))))))))) and control(2)) or (mode and (not control(2)))))))))))) and control(0)) or (mode and (not control(0)))))))))))) and control(1)) or (mode and (not control(1)))))))))))) and control(0)) or (mode and (not control(0)))))));
    C(31) <= (A(30) and B_u(30)) or ((A(30) or B_u(30)) and ((A(29) and B_u(29)) or ((A(29) or B_u(29)) and ((A(28) and B_u(28)) or ((A(28) or B_u(28)) and ((((A(27) and B_u(27)) or ((A(27) or B_u(27)) and ((A(26) and B_u(26)) or ((A(26) or B_u(26)) and ((A(25) and B_u(25)) or ((A(25) or B_u(25)) and ((A(24) and B_u(24)) or ((A(24) or B_u(24)) and ((((A(23) and B_u(23)) or ((A(23) or B_u(23)) and ((A(22) and B_u(22)) or ((A(22) or B_u(22)) and ((A(21) and B_u(21)) or ((A(21) or B_u(21)) and ((A(20) and B_u(20)) or ((A(20) or B_u(20)) and ((((A(19) and B_u(19)) or ((A(19) or B_u(19)) and ((A(18) and B_u(18)) or ((A(18) or B_u(18)) and ((A(17) and B_u(17)) or ((A(17) or B_u(17)) and ((A(16) and B_u(16)) or ((A(16) or B_u(16)) and ((((A(15) and B_u(15)) or ((A(15) or B_u(15)) and ((A(14) and B_u(14)) or ((A(14) or B_u(14)) and ((A(13) and B_u(13)) or ((A(13) or B_u(13)) and ((A(12) and B_u(12)) or ((A(12) or B_u(12)) and ((((A(11) and B_u(11)) or ((A(11) or B_u(11)) and ((A(10) and B_u(10)) or ((A(10) or B_u(10)) and ((A(9) and B_u(9)) or ((A(9) or B_u(9)) and ((A(8) and B_u(8)) or ((A(8) or B_u(8)) and ((((A(7) and B_u(7)) or ((A(7) or B_u(7)) and ((A(6) and B_u(6)) or ((A(6) or B_u(6)) and ((A(5) and B_u(5)) or ((A(5) or B_u(5)) and ((A(4) and B_u(4)) or ((A(4) or B_u(4)) and ((((A(3) and B_u(3)) or ((A(3) or B_u(3)) and ((A(2) and B_u(2)) or ((A(2) or B_u(2)) and ((A(1) and B_u(1)) or ((A(1) or B_u(1)) and ((A(0) and B_u(0)) or ((A(0) or B_u(0)) and (mode))))))))) and control(0)) or (mode and (not control(0)))))))))))) and control(1)) or (mode and (not control(1)))))))))))) and control(0)) or (mode and (not control(0)))))))))))) and control(2)) or (mode and (not control(2)))))))))))) and control(0)) or (mode and (not control(0)))))))))))) and control(1)) or (mode and (not control(1)))))))))))) and control(0)) or (mode and (not control(0)))))))));

end process Carrys;
process(A,B_u,C)
    begin
    for n in 0 to 31 loop
      S(n) <= (A(n)xor B_u(n)) xor C(n);
    end loop;
    end process;
end TypeArchitecture;

// VHDL entity IF_ID, as the project stores it:
--------------------------------------------------------------------------------
-- Project :
-- File    :
-- Autor   :
-- Date    :
--
--------------------------------------------------------------------------------
-- Description :
--
--------------------------------------------------------------------------------

LIBRARY ieee;
USE ieee.std_logic_1164.all;

ENTITY IF_ID IS
  PORT (
  ------------------------------------------------------------------------------
    pc, instruc        : IN  std_logic_vector(31 DOWNTO 0);
    clock, write_e              : IN std_logic;
    flush : IN std_logic;
    pcnext : IN std_logic_vector(31 DOWNTO 0);
    pc_o, instruc_o    : OUT std_logic_vector (31 DOWNTO 0);
    flush_next : OUT std_logic;
    pcnext_o : OUT std_logic_vector(31 DOWNTO 0));
END IF_ID;

--------------------------------------------------------------------------------
--Complete your VHDL description below
--------------------------------------------------------------------------------

ARCHITECTURE TypeArchitecture OF IF_ID IS
SIGNAL pc_mem,instruc_mem, pcnext_mem : std_logic_vector(31 DOWNTO 0);
BEGIN
PROCESS (clock,pc,instruc, flush, pcnext)
BEGIN
IF (write_e = '1') THEN
	IF (rising_edge(clock)) THEN
		pc_mem <= pc;
		instruc_mem <= instruc;
		pcnext_mem <= pcnext;
	END IF;
	IF (falling_edge(clock)) THEN
		IF (flush = '1') THEN 
			flush_next <= '1';
		ELSE
			flush_next <= '0';
			pc_o <= pc_mem;
			instruc_o <= instruc_mem;
			pcnext_o <= pcnext_mem;
		END IF;
	END IF;
END IF;

END PROCESS;
END TypeArchitecture;

// VHDL entity Imm_gen, as the project stores it:
--------------------------------------------------------------------------------
-- Project :
-- File    :
-- Autor   :
-- Date    :
--
--------------------------------------------------------------------------------
-- Description :
--
--------------------------------------------------------------------------------

LIBRARY ieee;
USE ieee.std_logic_1164.all;
USE ieee.numeric_std.all;

ENTITY Imm_gen IS
  PORT (
    instruc        : IN  std_logic_vector(31 DOWNTO 0);
    imm            : OUT std_logic_vector(31 DOWNTO 0)
    );
END Imm_gen;

--------------------------------------------------------------------------------
--Complete your VHDL description below
--------------------------------------------------------------------------------

ARCHITECTURE Behavioral OF Imm_gen IS
SIGNAL opcode : std_logic_vector (6 DOWNTO 0);
SIGNAL temp_imm: std_logic_vector (31 DOWNTO 0);
BEGIN
process(opcode,instruc,temp_imm)
begin
opcode (6 DOWNTO 0) <= instruc(6 DOWNTO 0);
temp_imm <= (others => '0');
IF (opcode = "0000011" OR opcode = "0010011" OR opcode = "0010000" OR opcode = "0010001" OR opcode = "0010010") THEN --Tipo I
	temp_imm (11 DOWNTO 0) <= instruc (31 DOWNTO 20);
	temp_imm (31 DOWNTO 12) <= (31 DOWNTO 12 => instruc(31));
ELSIF (opcode = "0100011") THEN --Tipo S
	temp_imm (11 DOWNTO 5) <= instruc (31 DOWNTO 25);
	temp_imm (4 DOWNTO 0) <= instruc (11 DOWNTO 7);
	temp_imm (31 DOWNTO 12) <= (31 DOWNTO 12 => instruc(31));

ELSIF (opcode = "1100011") THEN --Tipo SB
	temp_imm (12) <= instruc(31);
	temp_imm (11) <= instruc(7);
	temp_imm (10 DOWNTO 5) <= instruc (30 DOWNTO 25);
	temp_imm (4 DOWNTO 1) <= instruc (11 DOWNTO 8);
	temp_imm (31 DOWNTO 13) <= (31 DOWNTO 13 => instruc(31));
ELSIF(opcode = "0110111" OR opcode = "0010111") THEN --Tipo U
	temp_imm (31 DOWNTO 12) <= instruc(31 DOWNTO 12);
ELSIF(opcode = "1101111" OR opcode = "0010100" OR opcode = "0010101" OR opcode = "0010110") THEN --Tipo UJ
	temp_imm(20) <= instruc(31);
	temp_imm(10 DOWNTO 1) <= instruc(30 DOWNTO 21);
	temp_imm(11) <= instruc(20);
	temp_imm(19 DOWNTO 12) <= instruc(19 DOWNTO 12);
	temp_imm(31 DOWNTO 21) <= (31 DOWNTO 21 => instruc(31));
ELSE
	temp_imm(31 DOWNTO 0) <= "11111111111111111111111111111111";
END IF;
imm  <= temp_imm;
END process;
imm <= temp_imm;
END Behavioral;

// VHDL entity Control, as the project stores it:
--------------------------------------------------------------------------------
-- Project :
-- File    :
-- Autor   :
-- Date    :
--
--------------------------------------------------------------------------------
-- Description :
--
--------------------------------------------------------------------------------

LIBRARY ieee;
USE ieee.std_logic_1164.all;

ENTITY Control IS
  PORT (
    opcode        : IN  std_logic_vector(6 DOWNTO 0);
    nop : IN std_logic;
    func3 : IN std_logic_vector(2 DOWNTO 0);
    regwrite, alusrc, memread, memwrite, memtoreg, lui : OUT std_logic;
    aluop,branch       : OUT std_logic_vector(1 DOWNTO 0);
    jalr, auipc : OUT std_logic
    
    );
END Control;

ARCHITECTURE TypeArchitecture OF Control IS
BEGIN

PROCESS(opcode, nop)
BEGIN
IF (nop = '1') THEN
	aluop <= "00";
	regwrite <= '0';
	alusrc <= '0';
	memread <= '0';
	memwrite <= '0';
	memtoreg <= '0';
	branch <= "00";
	lui <= '0';
	jalr <= '0';
	auipc <= '0';
ELSE
case opcode is
when "0110011"|"0110000"|"0110001"|"0110010" => --Tipo R
	aluop <= "10";
	regwrite <= '1';
	alusrc <= '0';
	memread <= '0';
	memwrite <= '0';
	memtoreg <= '0';
	branch <= "00";
	lui <= '0';
	jalr <= '0';
	auipc <= '0';
when "0010011"|"0010000"|"0010001"|"0010010" => --Tipo I
	aluop <= "10";
	regwrite <= '1';
	alusrc <= '1';
	memread <= '0';
	memwrite <= '0';
	memtoreg <= '0';
	branch <= "00";
	lui <= '0';
	jalr <= '0';
	auipc <= '0';
when "1100011" => --bne e beq
	aluop <= "01";
	regwrite <= '0';
	alusrc <= '0';
	memread <= '0';
	memwrite <= '0';
	memtoreg <= '0';
	lui <= '0';
	jalr <= '0';
	auipc <= '0';
	IF (func3 = "000") THEN --beq
		branch <= "01";
	ELSIF (func3 = "001") THEN --bne
		branch <= "10";
	END IF;
when "1101111" => --jal
	aluop <= "01";
	regwrite <= '1';
	alusrc <= '0';
	memread <= '0';
	memwrite <= '0';
	memtoreg <= '0';
	branch <= "11";
	lui <= '0';
	jalr <= '0';
	auipc <= '0';

when "1100111" => --jalr
	aluop <= "01";
	regwrite <= '1';
	alusrc <= '0';
	memread <= '0';
	memwrite <= '0';
	memtoreg <= '0';
	branch <= "11";
	lui <= '0';
	jalr <= '1';
	auipc <= '0';

when "0000011" => --lw
	aluop <= "00";
	regwrite <= '1';
	alusrc <= '1';
	memread <= '1';
	memwrite <= '0';
	memtoreg <= '1';
	branch <= "00";
	lui <= '0';
	jalr <= '0';
	auipc <= '0';
when "0100011" =>--sw
	aluop <= "00";
	regwrite <= '0';
	alusrc <= '1';
	memread <= '0';
	memwrite <= '1';
	memtoreg <= '0';
	branch <= "00";
	lui <= '0';
	jalr <= '0';
	auipc <= '0';
when "0110111" => --lui
	aluop <= "00";
	regwrite <= '1';
	alusrc <= '1';
	memread <= '0';
	memwrite <= '0';
	memtoreg <= '0';
	branch <= "00";
	lui <= '1';
	jalr <= '0';
	auipc <= '0';
when "0010111"|"0010100"|"0010101"|"0010110" =>--auipc
	aluop <= "00";
	regwrite <= '1';
	alusrc <= '1';
	memread <= '0';
	memwrite <= '0';
	memtoreg <= '0';
	branch <= "00";
	lui <= '0';
	jalr <= '0';
	auipc <= '1';
when others =>
	aluop <= "00";
	regwrite <= '0';
	alusrc <= '1';
	memread <= '0';
	memwrite <= '0';
	memtoreg <= '0';
	branch <= "00";
	lui <= '0';
	jalr <= '0';
	auipc <= '0';
END case;
END IF;
END PROCESS;
END TypeArchitecture;

// VHDL entity Branch_ctrl, as the project stores it:
--------------------------------------------------------------------------------
-- Project :
-- File    :
-- Autor   :
-- Date    :
--
--------------------------------------------------------------------------------
-- Description :
--
--------------------------------------------------------------------------------

LIBRARY ieee;
USE ieee.std_logic_1164.all;

ENTITY Branch_ctrl IS
  PORT (
    aluzero : IN std_logic;
    branch : IN  std_logic_vector(1 DOWNTO 0);
    pcsrc        : OUT std_logic
    );
END Branch_ctrl;

--------------------------------------------------------------------------------
--Complete your VHDL description below
--------------------------------------------------------------------------------

ARCHITECTURE TypeArchitecture OF Branch_ctrl IS

BEGIN

PROCESS (branch,aluzero)
BEGIN
IF (branch = "00") THEN
	pcsrc <= '0';
ELSIF (branch = "11") THEN
	pcsrc <= '1';
ELSIF (branch = "01") THEN
	pcsrc <= aluzero;
ELSIF(branch = "10") THEN 
	pcsrc <= NOT(aluzero);
ELSE
	pcsrc <= '0';
END IF;
END PROCESS;
		

END TypeArchitecture;

// VHDL entity CARRY_LOOKAHEAD, as the project stores it:
--------------------------------------------------------------------------------
-- Project :
-- File    :
-- Autor   :
-- Date    :
--
--------------------------------------------------------------------------------
-- Description :
--
--------------------------------------------------------------------------------

library IEEE;

use ieee.std_logic_1164.all;
use ieee.numeric_std.all;

 entity CARRY_LOOKAHEAD is

  port(A, B : in std_logic_vector (31 downto 0);
  mode: in std_logic;
  Vec_size: in std_logic_vector(1 downto 0);
  S : out std_logic_vector (31 downto 0));

 end CARRY_LOOKAHEAD;

 architecture TypeArchitecture of CARRY_LOOKAHEAD is
 signal C     : std_logic_vector (31 downto 0);
 signal B_u     : std_logic_vector (31 downto 0);
 signal control  : std_logic_vector (2 downto 0);
 begin
 
--Esse código transoforma o número B em negativo, caso a operação seja a subtração A+(-B)
    process(B, mode)
    begin
    for n in 0 to 31 loop
      B_u(n) <= (B(n) and (not mode)) or ((not B(n)) and mode);
    end loop;
    end process;
    
-- Definindo control
    control(0) <= Vec_size(0) or Vec_size(1);
    control(1) <= Vec_size(1);
    control(2) <= Vec_size(0) and Vec_size(1);
    
Carrys:process(C,mode)
begin
    C(0) <= mode;
    C(1) <= (A(0) and B_u(0)) or ((A(0) or B_u(0)) and (mode));
    C(2) <= (A(1) and B_u(1)) or ((A(1) or B_u(1)) and ((A(0) and B_u(0)) or ((A(0) or B_u(0)) and (mode))));
    C(3) <= (A(2) and B_u(2)) or ((A(2) or B_u(2)) and ((A(1) and B_u(1)) or ((A(1) or B_u(1)) and ((A(0) and B_u(0)) or ((A(0) or B_u(0)) and (mode))))));
    -- Subcampo 1 de 4 bits
    C(4) <= (((A(3) and B_u(3)) or ((A(3) or B_u(3)) and ((A(2) and B_u(2)) or ((A(2) or B_u(2)) and ((A(1) and B_u(1)) or ((A(1) or B_u(1)) and ((A(0) and B_u(0)) or ((A(0) or B_u(0)) and (mode))))))))) and control(0)) or (mode and (not control(0)));
    C(5) <= (A(4) and B_u(4)) or ((A(4) or B_u(4)) and ((((A(3) and B_u(3)) or ((A(3) or B_u(3)) and ((A(2) and B_u(2)) or ((A(2) or B_u(2)) and ((A(1) and B_u(1)) or ((A(1) or B_u(1)) and ((A(0) and B_u(0)) or ((A(0) or B_u(0)) and (mode))))))))) and control(0)) or (mode and (not control(0)))));
    C(6) <= (A(5) and B_u(5)) or ((A(5) or B_u(5)) and ((A(4) and B_u(4)) or ((A(4) or B_u(4)) and ((((A(3) and B_u(3)) or ((A(3) or B_u(3)) and ((A(2) and B_u(2)) or ((A(2) or B_u(2)) and ((A(1) and B_u(1)) or ((A(1) or B_u(1)) and ((A(0) and B_u(0)) or ((A(0) or B_u(0)) and (mode))))))))) and control(0)) or (mode and (not control(0)))))));
    C(7) <= (A(6) and B_u(6)) or ((A(6) or B_u(6)) and ((A(5) and B_u(5)) or ((A(5) or B_u(5)) and ((A(4) and B_u(4)) or ((A(4) or B_u(4)) and ((((A(3) and B_u(3)) or ((A(3) or B_u(3)) and ((A(2) and B_u(2)) or ((A(2) or B_u(2)) and ((A(1) and B_u(1)) or ((A(1) or B_u(1)) and ((A(0) and B_u(0)) or ((A(0) or B_u(0)) and (mode))))))))) and control(0)) or (mode and (not control(0)))))))));
    -- Subcampo 2 de 4 bits
    C(8) <= (((A(7) and B_u(7)) or ((A(7) or B_u(7)) and ((A(6) and B_u(6)) or ((A(6) or B_u(6)) and ((A(5) and B_u(5)) or ((A(5) or B_u(5)) and ((A(4) and B_u(4)) or ((A(4) or B_u(4)) and ((((A(3) and B_u(3)) or ((A(3) or B_u(3)) and ((A(2) and B_u(2)) or ((A(2) or B_u(2)) and ((A(1) and B_u(1)) or ((A(1) or B_u(1)) and ((A(0) and B_u(0)) or ((A(0) or B_u(0)) and (mode))))))))) and control(0)) or (mode and (not control(0)))))))))))) and control(1)) or (mode and (not control(1)));
    C(9) <= (A(8) and B_u(8)) or ((A(8) or B_u(8)) and ((((A(7) and B_u(7)) or ((A(7) or B_u(7)) and ((A(6) and B_u(6)) or ((A(6) or B_u(6)) and ((A(5) and B_u(5)) or ((A(5) or B_u(5)) and ((A(4) and B_u(4)) or ((A(4) or B_u(4)) and ((((A(3) and B_u(3)) or ((A(3) or B_u(3)) and ((A(2) and B_u(2)) or ((A(2) or B_u(2)) and ((A(1) and B_u(1)) or ((A(1) or B_u(1)) and ((A(0) and B_u(0)) or ((A(0) or B_u(0)) and (mode))))))))) and control(0)) or (mode and (not control(0)))))))))))) and control(1)) or (mode and (not control(1)))));
    C(10) <= (A(9) and B_u(9)) or ((A(9) or B_u(9)) and ((A(8) and B_u(8)) or ((A(8) or B_u(8)) and ((((A(7) and B_u(7)) or ((A(7) or B_u(7)) and ((A(6) and B_u(6)) or ((A(6) or B_u(6)) and ((A(5) and B_u(5)) or ((A(5) or B_u(5)) and ((A(4) and B_u(4)) or ((A(4) or B_u(4)) and ((((A(3) and B_u(3)) or ((A(3) or B_u(3)) and ((A(2) and B_u(2)) or ((A(2) or B_u(2)) and ((A(1) and B_u(1)) or ((A(1) or B_u(1)) and ((A(0) and B_u(0)) or ((A(0) or B_u(0)) and (mode))))))))) and control(0)) or (mode and (not control(0)))))))))))) and control(1)) or (mode and (not control(1)))))));
    C(11) <= (A(10) and B_u(10)) or ((A(10) or B_u(10)) and ((A(9) and B_u(9)) or ((A(9) or B_u(9)) and ((A(8) and B_u(8)) or ((A(8) or B_u(8)) and ((((A(7) and B_u(7)) or ((A(7) or B_u(7)) and ((A(6) and B_u(6)) or ((A(6) or B_u(6)) and ((A(5) and B_u(5)) or ((A(5) or B_u(5)) and ((A(4) and B_u(4)) or ((A(4) or B_u(4)) and ((((A(3) and B_u(3)) or ((A(3) or B_u(3)) and ((A(2) and B_u(2)) or ((A(2) or B_u(2)) and ((A(1) and B_u(1)) or ((A(1) or B_u(1)) and ((A(0) and B_u(0)) or ((A(0) or B_u(0)) and (mode))))))))) and control(0)) or (mode and (not control(0)))))))))))) and control(1)) or (mode and (not control(1)))))))));
    -- Subcampo 3 de 4 bits
    C(12) <= (((A(11) and B_u(11)) or ((A(11) or B_u(11)) and ((A(10) and B_u(10)) or ((A(10) or B_u(10)) and ((A(9) and B_u(9)) or ((A(9) or B_u(9)) and ((A(8) and B_u(8)) or ((A(8) or B_u(8)) and ((((A(7) and B_u(7)) or ((A(7) or B_u(7)) and ((A(6) and B_u(6)) or ((A(6) or B_u(6)) and ((A(5) and B_u(5)) or ((A(5) or B_u(5)) and ((A(4) and B_u(4)) or ((A(4) or B_u(4)) and ((((A(3) and B_u(3)) or ((A(3) or B_u(3)) and ((A(2) and B_u(2)) or ((A(2) or B_u(2)) and ((A(1) and B_u(1)) or ((A(1) or B_u(1)) and ((A(0) and B_u(0)) or ((A(0) or B_u(0)) and (mode))))))))) and control(0)) or (mode and (not control(0)))))))))))) and control(1)) or (mode and (not control(1)))))))))))) and control(0)) or (mode and (not control(0)));
    C(13) <= (A(12) and B_u(12)) or ((A(12) or B_u(12)) and ((((A(11) and B_u(11)) or ((A(11) or B_u(11)) and ((A(10) and B_u(10)) or ((A(10) or B_u(10)) and ((A(9) and B_u(9)) or ((A(9) or B_u(9)) and ((A(8) and B_u(8)) or ((A(8) or B_u(8)) and ((((A(7) and B_u(7)) or ((A(7) or B_u(7)) and ((A(6) and B_u(6)) or ((A(6) or B_u(6)) and ((A(5) and B_u(5)) or ((A(5) or B_u(5)) and ((A(4) and B_u(4)) or ((A(4) or B_u(4)) and ((((A(3) and B_u(3)) or ((A(3) or B_u(3)) and ((A(2) and B_u(2)) or ((A(2) or B_u(2)) and ((A(1) and B_u(1)) or ((A(1) or B_u(1)) and ((A(0) and B_u(0)) or ((A(0) or B_u(0)) and (mode))))))))) and control(0)) or (mode and (not control(0)))))))))))) and control(1)) or (mode and (not control(1)))))))))))) and control(0)) or (mode and (not control(0)))));
    C(14) <= (A(13) and B_u(13)) or ((A(13) or B_u(13)) and ((A(12) and B_u(12)) or ((A(12) or B_u(12)) and ((((A(11) and B_u(11)) or ((A(11) or B_u(11)) and ((A(10) and B_u(10)) or ((A(10) or B_u(10)) and ((A(9) and B_u(9)) or ((A(9) or B_u(9)) and ((A(8) and B_u(8)) or ((A(8) or B_u(8)) and ((((A(7) and B_u(7)) or ((A(7) or B_u(7)) and ((A(6) and B_u(6)) or ((A(6) or B_u(6)) and ((A(5) and B_u(5)) or ((A(5) or B_u(5)) and ((A(4) and B_u(4)) or ((A(4) or B_u(4)) and ((((A(3) and B_u(3)) or ((A(3) or B_u(3)) and ((A(2) and B_u(2)) or ((A(2) or B_u(2)) and ((A(1) and B_u(1)) or ((A(1) or B_u(1)) and ((A(0) and B_u(0)) or ((A(0) or B_u(0)) and (mode))))))))) and control(0)) or (mode and (not control(0)))))))))))) and control(1)) or (mode and (not control(1)))))))))))) and control(0)) or (mode and (not control(0)))))));
    C(15) <= (A(14) and B_u(14)) or ((A(14) or B_u(14)) and ((A(13) and B_u(13)) or ((A(13) or B_u(13)) and ((A(12) and B_u(12)) or ((A(12) or B_u(12)) and ((((A(11) and B_u(11)) or ((A(11) or B_u(11)) and ((A(10) and B_u(10)) or ((A(10) or B_u(10)) and ((A(9) and B_u(9)) or ((A(9) or B_u(9)) and ((A(8) and B_u(8)) or ((A(8) or B_u(8)) and ((((A(7) and B_u(7)) or ((A(7) or B_u(7)) and ((A(6) and B_u(6)) or ((A(6) or B_u(6)) and ((A(5) and B_u(5)) or ((A(5) or B_u(5)) and ((A(4) and B_u(4)) or ((A(4) or B_u(4)) and ((((A(3) and B_u(3)) or ((A(3) or B_u(3)) and ((A(2) and B_u(2)) or ((A(2) or B_u(2)) and ((A(1) and B_u(1)) or ((A(1) or B_u(1)) and ((A(0) and B_u(0)) or ((A(0) or B_u(0)) and (mode))))))))) and control(0)) or (mode and (not control(0)))))))))))) and control(1)) or (mode and (not control(1)))))))))))) and control(0)) or (mode and (not control(0)))))))));
    -- Subcampo 4 de 4 bits
    C(16) <= (((A(15) and B_u(15)) or ((A(15) or B_u(15)) and ((A(14) and B_u(14)) or ((A(14) or B_u(14)) and ((A(13) and B_u(13)) or ((A(13) or B_u(13)) and ((A(12) and B_u(12)) or ((A(12) or B_u(12)) and ((((A(11) and B_u(11)) or ((A(11) or B_u(11)) and ((A(10) and B_u(10)) or ((A(10) or B_u(10)) and ((A(9) and B_u(9)) or ((A(9) or B_u(9)) and ((A(8) and B_u(8)) or ((A(8) or B_u(8)) and ((((A(7) and B_u(7)) or ((A(7) or B_u(7)) and ((A(6) and B_u(6)) or ((A(6) or B_u(6)) and ((A(5) and B_u(5)) or ((A(5) or B_u(5)) and ((A(4) and B_u(4)) or ((A(4) or B_u(4)) and ((((A(3) and B_u(3)) or ((A(3) or B_u(3)) and ((A(2) and B_u(2)) or ((A(2) or B_u(2)) and ((A(1) and B_u(1)) or ((A(1) or B_u(1)) and ((A(0) and B_u(0)) or ((A(0) or B_u(0)) and (mode))))))))) and control(0)) or (mode and (not control(0)))))))))))) and control(1)) or (mode and (not control(1)))))))))))) and control(0)) or (mode and (not control(0)))))))))))) and control(2)) or (mode and (not control(2)));
    C(17) <= (A(16) and B_u(16)) or ((A(16) or B_u(16)) and ((((A(15) and B_u(15)) or ((A(15) or B_u(15)) and ((A(14) and B_u(14)) or ((A(14) or B_u(14)) and ((A(13) and B_u(13)) or ((A(13) or B_u(13)) and ((A(12) and B_u(12)) or ((A(12) or B_u(12)) and ((((A(11) and B_u(11)) or ((A(11) or B_u(11)) and ((A(10) and B_u(10)) or ((A(10) or B_u(10)) and ((A(9) and B_u(9)) or ((A(9) or B_u(9)) and ((A(8) and B_u(8)) or ((A(8) or B_u(8)) and ((((A(7) and B_u(7)) or ((A(7) or B_u(7)) and ((A(6) and B_u(6)) or ((A(6) or B_u(6)) and ((A(5) and B_u(5)) or ((A(5) or B_u(5)) and ((A(4) and B_u(4)) or ((A(4) or B_u(4)) and ((((A(3) and B_u(3)) or ((A(3) or B_u(3)) and ((A(2) and B_u(2)) or ((A(2) or B_u(2)) and ((A(1) and B_u(1)) or ((A(1) or B_u(1)) and ((A(0) and B_u(0)) or ((A(0) or B_u(0)) and (mode))))))))) and control(0)) or (mode and (not control(0)))))))))))) and control(1)) or (mode and (not control(1)))))))))))) and control(0)) or (mode and (not control(0)))))))))))) and control(2)) or (mode and (not control(2)))));
    C(18) <= (A(17) and B_u(17)) or ((A(17) or B_u(17)) and ((A(16) and B_u(16)) or ((A(16) or B_u(16)) and ((((A(15) and B_u(15)) or ((A(15) or B_u(15)) and ((A(14) and B_u(14)) or ((A(14) or B_u(14)) and ((A(13) and B_u(13)) or ((A(13) or B_u(13)) and ((A(12) and B_u(12)) or ((A(12) or B_u(12)) and ((((A(11) and B_u(11)) or ((A(11) or B_u(11)) and ((A(10) and B_u(10)) or ((A(10) or B_u(10)) and ((A(9) and B_u(9)) or ((A(9) or B_u(9)) and ((A(8) and B_u(8)) or ((A(8) or B_u(8)) and ((((A(7) and B_u(7)) or ((A(7) or B_u(7)) and ((A(6) and B_u(6)) or ((A(6) or B_u(6)) and ((A(5) and B_u(5)) or ((A(5) or B_u(5)) and ((A(4) and B_u(4)) or ((A(4) or B_u(4)) and ((((A(3) and B_u(3)) or ((A(3) or B_u(3)) and ((A(2) and B_u(2)) or ((A(2) or B_u(2)) and ((A(1) and B_u(1)) or ((A(1) or B_u(1)) and ((A(0) and B_u(0)) or ((A(0) or B_u(0)) and (mode))))))))) and control(0)) or (mode and (not control(0)))))))))))) and control(1)) or (mode and (not control(1)))))))))))) and control(0)) or (mode and (not control(0)))))))))))) and control(2)) or (mode and (not control(2)))))));
    C(19) <= (A(18) and B_u(18)) or ((A(18) or B_u(18)) and ((A(17) and B_u(17)) or ((A(17) or B_u(17)) and ((A(16) and B_u(16)) or ((A(16) or B_u(16)) and ((((A(15) and B_u(15)) or ((A(15) or B_u(15)) and ((A(14) and B_u(14)) or ((A(14) or B_u(14)) and ((A(13) and B_u(13)) or ((A(13) or B_u(13)) and ((A(12) and B_u(12)) or ((A(12) or B_u(12)) and ((((A(11) and B_u(11)) or ((A(11) or B_u(11)) and ((A(10) and B_u(10)) or ((A(10) or B_u(10)) and ((A(9) and B_u(9)) or ((A(9) or B_u(9)) and ((A(8) and B_u(8)) or ((A(8) or B_u(8)) and ((((A(7) and B_u(7)) or ((A(7) or B_u(7)) and ((A(6) and B_u(6)) or ((A(6) or B_u(6)) and ((A(5) and B_u(5)) or ((A(5) or B_u(5)) and ((A(4) and B_u(4)) or ((A(4) or B_u(4)) and ((((A(3) and B_u(3)) or ((A(3) or B_u(3)) and ((A(2) and B_u(2)) or ((A(2) or B_u(2)) and ((A(1) and B_u(1)) or ((A(1) or B_u(1)) and ((A(0) and B_u(0)) or ((A(0) or B_u(0)) and (mode))))))))) and control(0)) or (mode and (not control(0)))))))))))) and control(1)) or (mode and (not control(1)))))))))))) and control(0)) or (mode and (not control(0)))))))))))) and control(2)) or (mode and (not control(2)))))))));
    -- Subcampo 5 de 4 bits
    C(20) <= (((A(19) and B_u(19)) or ((A(19) or B_u(19)) and ((A(18) and B_u(18)) or ((A(18) or B_u(18)) and ((A(17) and B_u(17)) or ((A(17) or B_u(17)) and ((A(16) and B_u(16)) or ((A(16) or B_u(16)) and ((((A(15) and B_u(15)) or ((A(15) or B_u(15)) and ((A(14) and B_u(14)) or ((A(14) or B_u(14)) and ((A(13) and B_u(13)) or ((A(13) or B_u(13)) and ((A(12) and B_u(12)) or ((A(12) or B_u(12)) and ((((A(11) and B_u(11)) or ((A(11) or B_u(11)) and ((A(10) and B_u(10)) or ((A(10) or B_u(10)) and ((A(9) and B_u(9)) or ((A(9) or B_u(9)) and ((A(8) and B_u(8)) or ((A(8) or B_u(8)) and ((((A(7) and B_u(7)) or ((A(7) or B_u(7)) and ((A(6) and B_u(6)) or ((A(6) or B_u(6)) and ((A(5) and B_u(5)) or ((A(5) or B_u(5)) and ((A(4) and B_u(4)) or ((A(4) or B_u(4)) and ((((A(3) and B_u(3)) or ((A(3) or B_u(3)) and ((A(2) and B_u(2)) or ((A(2) or B_u(2)) and ((A(1) and B_u(1)) or ((A(1) or B_u(1)) and ((A(0) and B_u(0)) or ((A(0) or B_u(0)) and (mode))))))))) and control(0)) or (mode and (not control(0)))))))))))) and control(1)) or (mode and (not control(1)))))))))))) and control(0)) or (mode and (not control(0)))))))))))) and control(2)) or (mode and (not control(2)))))))))))) and control(0)) or (mode and (not control(0)));
    C(21) <= (A(20) and B_u(20)) or ((A(20) or B_u(20)) and ((((A(19) and B_u(19)) or ((A(19) or B_u(19)) and ((A(18) and B_u(18)) or ((A(18) or B_u(18)) and ((A(17) and B_u(17)) or ((A(17) or B_u(17)) and ((A(16) and B_u(16)) or ((A(16) or B_u(16)) and ((((A(15) and B_u(15)) or ((A(15) or B_u(15)) and ((A(14) and B_u(14)) or ((A(14) or B_u(14)) and ((A(13) and B_u(13)) or ((A(13) or B_u(13)) and ((A(12) and B_u(12)) or ((A(12) or B_u(12)) and ((((A(11) and B_u(11)) or ((A(11) or B_u(11)) and ((A(10) and B_u(10)) or ((A(10) or B_u(10)) and ((A(9) and B_u(9)) or ((A(9) or B_u(9)) and ((A(8) and B_u(8)) or ((A(8) or B_u(8)) and ((((A(7) and B_u(7)) or ((A(7) or B_u(7)) and ((A(6) and B_u(6)) or ((A(6) or B_u(6)) and ((A(5) and B_u(5)) or ((A(5) or B_u(5)) and ((A(4) and B_u(4)) or ((A(4) or B_u(4)) and ((((A(3) and B_u(3)) or ((A(3) or B_u(3)) and ((A(2) and B_u(2)) or ((A(2) or B_u(2)) and ((A(1) and B_u(1)) or ((A(1) or B_u(1)) and ((A(0) and B_u(0)) or ((A(0) or B_u(0)) and (mode))))))))) and control(0)) or (mode and (not control(0)))))))))))) and control(1)) or (mode and (not control(1)))))))))))) and control(0)) or (mode and (not control(0)))))))))))) and control(2)) or (mode and (not control(2)))))))))))) and control(0)) or (mode and (not control(0)))));
    C(22) <= (A(21) and B_u(21)) or ((A(21) or B_u(21)) and ((A(20) and B_u(20)) or ((A(20) or B_u(20)) and ((((A(19) and B_u(19)) or ((A(19) or B_u(19)) and ((A(18) and B_u(18)) or ((A(18) or B_u(18)) and ((A(17) and B_u(17)) or ((A(17) or B_u(17)) and ((A(16) and B_u(16)) or ((A(16) or B_u(16)) and ((((A(15) and B_u(15)) or ((A(15) or B_u(15)) and ((A(14) and B_u(14)) or ((A(14) or B_u(14)) and ((A(13) and B_u(13)) or ((A(13) or B_u(13)) and ((A(12) and B_u(12)) or ((A(12) or B_u(12)) and ((((A(11) and B_u(11)) or ((A(11) or B_u(11)) and ((A(10) and B_u(10)) or ((A(10) or B_u(10)) and ((A(9) and B_u(9)) or ((A(9) or B_u(9)) and ((A(8) and B_u(8)) or ((A(8) or B_u(8)) and ((((A(7) and B_u(7)) or ((A(7) or B_u(7)) and ((A(6) and B_u(6)) or ((A(6) or B_u(6)) and ((A(5) and B_u(5)) or ((A(5) or B_u(5)) and ((A(4) and B_u(4)) or ((A(4) or B_u(4)) and ((((A(3) and B_u(3)) or ((A(3) or B_u(3)) and ((A(2) and B_u(2)) or ((A(2) or B_u(2)) and ((A(1) and B_u(1)) or ((A(1) or B_u(1)) and ((A(0) and B_u(0)) or ((A(0) or B_u(0)) and (mode))))))))) and control(0)) or (mode and (not control(0)))))))))))) and control(1)) or (mode and (not control(1)))))))))))) and control(0)) or (mode and (not control(0)))))))))))) and control(2)) or (mode and (not control(2)))))))))))) and control(0)) or (mode and (not control(0)))))));
    C(23) <= (A(22) and B_u(22)) or ((A(22) or B_u(22)) and ((A(21) and B_u(21)) or ((A(21) or B_u(21)) and ((A(20) and B_u(20)) or ((A(20) or B_u(20)) and ((((A(19) and B_u(19)) or ((A(19) or B_u(19)) and ((A(18) and B_u(18)) or ((A(18) or B_u(18)) and ((A(17) and B_u(17)) or ((A(17) or B_u(17)) and ((A(16) and B_u(16)) or ((A(16) or B_u(16)) and ((((A(15) and B_u(15)) or ((A(15) or B_u(15)) and ((A(14) and B_u(14)) or ((A(14) or B_u(14)) and ((A(13) and B_u(13)) or ((A(13) or B_u(13)) and ((A(12) and B_u(12)) or ((A(12) or B_u(12)) and ((((A(11) and B_u(11)) or ((A(11) or B_u(11)) and ((A(10) and B_u(10)) or ((A(10) or B_u(10)) and ((A(9) and B_u(9)) or ((A(9) or B_u(9)) and ((A(8) and B_u(8)) or ((A(8) or B_u(8)) and ((((A(7) and B_u(7)) or ((A(7) or B_u(7)) and ((A(6) and B_u(6)) or ((A(6) or B_u(6)) and ((A(5) and B_u(5)) or ((A(5) or B_u(5)) and ((A(4) and B_u(4)) or ((A(4) or B_u(4)) and ((((A(3) and B_u(3)) or ((A(3) or B_u(3)) and ((A(2) and B_u(2)) or ((A(2) or B_u(2)) and ((A(1) and B_u(1)) or ((A(1) or B_u(1)) and ((A(0) and B_u(0)) or ((A(0) or B_u(0)) and (mode))))))))) and control(0)) or (mode and (not control(0)))))))))))) and control(1)) or (mode and (not control(1)))))))))))) and control(0)) or (mode and (not control(0)))))))))))) and control(2)) or (mode and (not control(2)))))))))))) and control(0)) or (mode and (not control(0)))))))));
    -- Subcampo 6 de 4 bits
    C(24) <= (((A(23) and B_u(23)) or ((A(23) or B_u(23)) and ((A(22) and B_u(22)) or ((A(22) or B_u(22)) and ((A(21) and B_u(21)) or ((A(21) or B_u(21)) and ((A(20) and B_u(20)) or ((A(20) or B_u(20)) and ((((A(19) and B_u(19)) or ((A(19) or B_u(19)) and ((A(18) and B_u(18)) or ((A(18) or B_u(18)) and ((A(17) and B_u(17)) or ((A(17) or B_u(17)) and ((A(16) and B_u(16)) or ((A(16) or B_u(16)) and ((((A(15) and B_u(15)) or ((A(15) or B_u(15)) and ((A(14) and B_u(14)) or ((A(14) or B_u(14)) and ((A(13) and B_u(13)) or ((A(13) or B_u(13)) and ((A(12) and B_u(12)) or ((A(12) or B_u(12)) and ((((A(11) and B_u(11)) or ((A(11) or B_u(11)) and ((A(10) and B_u(10)) or ((A(10) or B_u(10)) and ((A(9) and B_u(9)) or ((A(9) or B_u(9)) and ((A(8) and B_u(8)) or ((A(8) or B_u(8)) and ((((A(7) and B_u(7)) or ((A(7) or B_u(7)) and ((A(6) and B_u(6)) or ((A(6) or B_u(6)) and ((A(5) and B_u(5)) or ((A(5) or B_u(5)) and ((A(4) and B_u(4)) or ((A(4) or B_u(4)) and ((((A(3) and B_u(3)) or ((A(3) or B_u(3)) and ((A(2) and B_u(2)) or ((A(2) or B_u(2)) and ((A(1) and B_u(1)) or ((A(1) or B_u(1)) and ((A(0) and B_u(0)) or ((A(0) or B_u(0)) and (mode))))))))) and control(0)) or (mode and (not control(0)))))))))))) and control(1)) or (mode and (not control(1)))))))))))) and control(0)) or (mode and (not control(0)))))))))))) and control(2)) or (mode and (not control(2)))))))))))) and control(0)) or (mode and (not control(0)))))))))))) and control(1)) or (mode and (not control(1)));
    C(25) <= (A(24) and B_u(24)) or ((A(24) or B_u(24)) and ((((A(23) and B_u(23)) or ((A(23) or B_u(23)) and ((A(22) and B_u(22)) or ((A(22) or B_u(22)) and ((A(21) and B_u(21)) or ((A(21) or B_u(21)) and ((A(20) and B_u(20)) or ((A(20) or B_u(20)) and ((((A(19) and B_u(19)) or ((A(19) or B_u(19)) and ((A(18) and B_u(18)) or ((A(18) or B_u(18)) and ((A(17) and B_u(17)) or ((A(17) or B_u(17)) and ((A(16) and B_u(16)) or ((A(16) or B_u(16)) and ((((A(15) and B_u(15)) or ((A(15) or B_u(15)) and ((A(14) and B_u(14)) or ((A(14) or B_u(14)) and ((A(13) and B_u(13)) or ((A(13) or B_u(13)) and ((A(12) and B_u(12)) or ((A(12) or B_u(12)) and ((((A(11) and B_u(11)) or ((A(11) or B_u(11)) and ((A(10) and B_u(10)) or ((A(10) or B_u(10)) and ((A(9) and B_u(9)) or ((A(9) or B_u(9)) and ((A(8) and B_u(8)) or ((A(8) or B_u(8)) and ((((A(7) and B_u(7)) or ((A(7) or B_u(7)) and ((A(6) and B_u(6)) or ((A(6) or B_u(6)) and ((A(5) and B_u(5)) or ((A(5) or B_u(5)) and ((A(4) and B_u(4)) or ((A(4) or B_u(4)) and ((((A(3) and B_u(3)) or ((A(3) or B_u(3)) and ((A(2) and B_u(2)) or ((A(2) or B_u(2)) and ((A(1) and B_u(1)) or ((A(1) or B_u(1)) and ((A(0) and B_u(0)) or ((A(0) or B_u(0)) and (mode))))))))) and control(0)) or (mode and (not control(0)))))))))))) and control(1)) or (mode and (not control(1)))))))))))) and control(0)) or (mode and (not control(0)))))))))))) and control(2)) or (mode and (not control(2)))))))))))) and control(0)) or (mode and (not control(0)))))))))))) and control(1)) or (mode and (not control(1)))));
    C(26) <= (A(25) and B_u(25)) or ((A(25) or B_u(25)) and ((A(24) and B_u(24)) or ((A(24) or B_u(24)) and ((((A(23) and B_u(23)) or ((A(23) or B_u(23)) and ((A(22) and B_u(22)) or ((A(22) or B_u(22)) and ((A(21) and B_u(21)) or ((A(21) or B_u(21)) and ((A(20) and B_u(20)) or ((A(20) or B_u(20)) and ((((A(19) and B_u(19)) or ((A(19) or B_u(19)) and ((A(18) and B_u(18)) or ((A(18) or B_u(18)) and ((A(17) and B_u(17)) or ((A(17) or B_u(17)) and ((A(16) and B_u(16)) or ((A(16) or B_u(16)) and ((((A(15) and B_u(15)) or ((A(15) or B_u(15)) and ((A(14) and B_u(14)) or ((A(14) or B_u(14)) and ((A(13) and B_u(13)) or ((A(13) or B_u(13)) and ((A(12) and B_u(12)) or ((A(12) or B_u(12)) and ((((A(11) and B_u(11)) or ((A(11) or B_u(11)) and ((A(10) and B_u(10)) or ((A(10) or B_u(10)) and ((A(9) and B_u(9)) or ((A(9) or B_u(9)) and ((A(8) and B_u(8)) or ((A(8) or B_u(8)) and ((((A(7) and B_u(7)) or ((A(7) or B_u(7)) and ((A(6) and B_u(6)) or ((A(6) or B_u(6)) and ((A(5) and B_u(5)) or ((A(5) or B_u(5)) and ((A(4) and B_u(4)) or ((A(4) or B_u(4)) and ((((A(3) and B_u(3)) or ((A(3) or B_u(3)) and ((A(2) and B_u(2)) or ((A(2) or B_u(2)) and ((A(1) and B_u(1)) or ((A(1) or B_u(1)) and ((A(0) and B_u(0)) or ((A(0) or B_u(0)) and (mode))))))))) and control(0)) or (mode and (not control(0)))))))))))) and control(1)) or (mode and (not control(1)))))))))))) and control(0)) or (mode and (not control(0)))))))))))) and control(2)) or (mode and (not control(2)))))))))))) and control(0)) or (mode and (not control(0)))))))))))) and control(1)) or (mode and (not control(1)))))));
    C(27) <= (A(26) and B_u(26)) or ((A(26) or B_u(26)) and ((A(25) and B_u(25)) or ((A(25) or B_u(25)) and ((A(24) and B_u(24)) or ((A(24) or B_u(24)) and ((((A(23) and B_u(23)) or ((A(23) or B_u(23)) and ((A(22) and B_u(22)) or ((A(22) or B_u(22)) and ((A(21) and B_u(21)) or ((A(21) or B_u(21)) and ((A(20) and B_u(20)) or ((A(20) or B_u(20)) and ((((A(19) and B_u(19)) or ((A(19) or B_u(19)) and ((A(18) and B_u(18)) or ((A(18) or B_u(18)) and ((A(17) and B_u(17)) or ((A(17) or B_u(17)) and ((A(16) and B_u(16)) or ((A(16) or B_u(16)) and ((((A(15) and B_u(15)) or ((A(15) or B_u(15)) and ((A(14) and B_u(14)) or ((A(14) or B_u(14)) and ((A(13) and B_u(13)) or ((A(13) or B_u(13)) and ((A(12) and B_u(12)) or ((A(12) or B_u(12)) and ((((A(11) and B_u(11)) or ((A(11) or B_u(11)) and ((A(10) and B_u(10)) or ((A(10) or B_u(10)) and ((A(9) and B_u(9)) or ((A(9) or B_u(9)) and ((A(8) and B_u(8)) or ((A(8) or B_u(8)) and ((((A(7) and B_u(7)) or ((A(7) or B_u(7)) and ((A(6) and B_u(6)) or ((A(6) or B_u(6)) and ((A(5) and B_u(5)) or ((A(5) or B_u(5)) and ((A(4) and B_u(4)) or ((A(4) or B_u(4)) and ((((A(3) and B_u(3)) or ((A(3) or B_u(3)) and ((A(2) and B_u(2)) or ((A(2) or B_u(2)) and ((A(1) and B_u(1)) or ((A(1) or B_u(1)) and ((A(0) and B_u(0)) or ((A(0) or B_u(0)) and (mode))))))))) and control(0)) or (mode and (not control(0)))))))))))) and control(1)) or (mode and (not control(1)))))))))))) and control(0)) or (mode and (not control(0)))))))))))) and control(2)) or (mode and (not control(2)))))))))))) and control(0)) or (mode and (not control(0)))))))))))) and control(1)) or (mode and (not control(1)))))))));
    -- Subcampo 7 de 4 bits
    C(28) <= (((A(27) and B_u(27)) or ((A(27) or B_u(27)) and ((A(26) and B_u(26)) or ((A(26) or B_u(26)) and ((A(25) and B_u(25)) or ((A(25) or B_u(25)) and ((A(24) and B_u(24)) or ((A(24) or B_u(24)) and ((((A(23) and B_u(23)) or ((A(23) or B_u(23)) and ((A(22) and B_u(22)) or ((A(22) or B_u(22)) and ((A(21) and B_u(21)) or ((A(21) or B_u(21)) and ((A(20) and B_u(20)) or ((A(20) or B_u(20)) and ((((A(19) and B_u(19)) or ((A(19) or B_u(19)) and ((A(18) and B_u(18)) or ((A(18) or B_u(18)) and ((A(17) and B_u(17)) or ((A(17) or B_u(17)) and ((A(16) and B_u(16)) or ((A(16) or B_u(16)) and ((((A(15) and B_u(15)) or ((A(15) or B_u(15)) and ((A(14) and B_u(14)) or ((A(14) or B_u(14)) and ((A(13) and B_u(13)) or ((A(13) or B_u(13)) and ((A(12) and B_u(12)) or ((A(12) or B_u(12)) and ((((A(11) and B_u(11)) or ((A(11) or B_u(11)) and ((A(10) and B_u(10)) or ((A(10) or B_u(10)) and ((A(9) and B_u(9)) or ((A(9) or B_u(9)) and ((A(8) and B_u(8)) or ((A(8) or B_u(8)) and ((((A(7) and B_u(7)) or ((A(7) or B_u(7)) and ((A(6) and B_u(6)) or ((A(6) or B_u(6)) and ((A(5) and B_u(5)) or ((A(5) or B_u(5)) and ((A(4) and B_u(4)) or ((A(4) or B_u(4)) and ((((A(3) and B_u(3)) or ((A(3) or B_u(3)) and ((A(2) and B_u(2)) or ((A(2) or B_u(2)) and ((A(1) and B_u(1)) or ((A(1) or B_u(1)) and ((A(0) and B_u(0)) or ((A(0) or B_u(0)) and (mode))))))))) and control(0)) or (mode and (not control(0)))))))))))) and control(1)) or (mode and (not control(1)))))))))))) and control(0)) or (mode and (not control(0)))))))))))) and control(2)) or (mode and (not control(2)))))))))))) and control(0)) or (mode and (not control(0)))))))))))) and control(1)) or (mode and (not control(1)))))))))))) and control(0)) or (mode and (not control(0)));
    C(29) <= (A(28) and B_u(28)) or ((A(28) or B_u(28)) and ((((A(27) and B_u(27)) or ((A(27) or B_u(27)) and ((A(26) and B_u(26)) or ((A(26) or B_u(26)) and ((A(25) and B_u(25)) or ((A(25) or B_u(25)) and ((A(24) and B_u(24)) or ((A(24) or B_u(24)) and ((((A(23) and B_u(23)) or ((A(23) or B_u(23)) and ((A(22) and B_u(22)) or ((A(22) or B_u(22)) and ((A(21) and B_u(21)) or ((A(21) or B_u(21)) and ((A(20) and B_u(20)) or ((A(20) or B_u(20)) and ((((A(19) and B_u(19)) or ((A(19) or B_u(19)) and ((A(18) and B_u(18)) or ((A(18) or B_u(18)) and ((A(17) and B_u(17)) or ((A(17) or B_u(17)) and ((A(16) and B_u(16)) or ((A(16) or B_u(16)) and ((((A(15) and B_u(15)) or ((A(15) or B_u(15)) and ((A(14) and B_u(14)) or ((A(14) or B_u(14)) and ((A(13) and B_u(13)) or ((A(13) or B_u(13)) and ((A(12) and B_u(12)) or ((A(12) or B_u(12)) and ((((A(11) and B_u(11)) or ((A(11) or B_u(11)) and ((A(10) and B_u(10)) or ((A(10) or B_u(10)) and ((A(9) and B_u(9)) or ((A(9) or B_u(9)) and ((A(8) and B_u(8)) or ((A(8) or B_u(8)) and ((((A(7) and B_u(7)) or ((A(7) or B_u(7)) and ((A(6) and B_u(6)) or ((A(6) or B_u(6)) and ((A(5) and B_u(5)) or ((A(5) or B_u(5)) and ((A(4) and B_u(4)) or ((A(4) or B_u(4)) and ((((A(3) and B_u(3)) or ((A(3) or B_u(3)) and ((A(2) and B_u(2)) or ((A(2) or B_u(2)) and ((A(1) and B_u(1)) or ((A(1) or B_u(1)) and ((A(0) and B_u(0)) or ((A(0) or B_u(0)) and (mode))))))))) and control(0)) or (mode and (not control(0)))))))))))) and control(1)) or (mode and (not control(1)))))))))))) and control(0)) or (mode and (not control(0)))))))))))) and control(2)) or (mode and (not control(2)))))))))))) and control(0)) or (mode and (not control(0)))))))))))) and control(1)) or (mode and (not control(1)))))))))))) and control(0)) or (mode and (not control(0)))));
    C(30) <= (A(29) and B_u(29)) or ((A(29) or B_u(29)) and ((A(28) and B_u(28)) or ((A(28) or B_u(28)) and ((((A(27) and B_u(27)) or ((A(27) or B_u(27)) and ((A(26) and B_u(26)) or ((A(26) or B_u(26)) and ((A(25) and B_u(25)) or ((A(25) or B_u(25)) and ((A(24) and B_u(24)) or ((A(24) or B_u(24)) and ((((A(23) and B_u(23)) or ((A(23) or B_u(23)) and ((A(22) and B_u(22)) or ((A(22) or B_u(22)) and ((A(21) and B_u(21)) or ((A(21) or B_u(21)) and ((A(20) and B_u(20)) or ((A(20) or B_u(20)) and ((((A(19) and B_u(19)) or ((A(19) or B_u(19)) and ((A(18) and B_u(18)) or ((A(18) or B_u(18)) and ((A(17) and B_u(17)) or ((A(17) or B_u(17)) and ((A(16) and B_u(16)) or ((A(16) or B_u(16)) and ((((A(15) and B_u(15)) or ((A(15) or B_u(15)) and ((A(14) and B_u(14)) or ((A(14) or B_u(14)) and ((A(13) and B_u(13)) or ((A(13) or B_u(13)) and ((A(12) and B_u(12)) or ((A(12) or B_u(12)) and ((((A(11) and B_u(11)) or ((A(11) or B_u(11)) and ((A(10) and B_u(10)) or ((A(10) or B_u(10)) and ((A(9) and B_u(9)) or ((A(9) or B_u(9)) and ((A(8) and B_u(8)) or ((A(8) or B_u(8)) and ((((A(7) and B_u(7)) or ((A(7) or B_u(7)) and ((A(6) and B_u(6)) or ((A(6) or B_u(6)) and ((A(5) and B_u(5)) or ((A(5) or B_u(5)) and ((A(4) and B_u(4)) or ((A(4) or B_u(4)) and ((((A(3) and B_u(3)) or ((A(3) or B_u(3)) and ((A(2) and B_u(2)) or ((A(2) or B_u(2)) and ((A(1) and B_u(1)) or ((A(1) or B_u(1)) and ((A(0) and B_u(0)) or ((A(0) or B_u(0)) and (mode))))))))) and control(0)) or (mode and (not control(0)))))))))))) and control(1)) or (mode and (not control(1)))))))))))) and control(0)) or (mode and (not control(0)))))))))))) and control(2)) or (mode and (not control(2)))))))))))) and control(0)) or (mode and (not control(0)))))))))))) and control(1)) or (mode and (not control(1)))))))))))) and control(0)) or (mode and (not control(0)))))));
    C(31) <= (A(30) and B_u(30)) or ((A(30) or B_u(30)) and ((A(29) and B_u(29)) or ((A(29) or B_u(29)) and ((A(28) and B_u(28)) or ((A(28) or B_u(28)) and ((((A(27) and B_u(27)) or ((A(27) or B_u(27)) and ((A(26) and B_u(26)) or ((A(26) or B_u(26)) and ((A(25) and B_u(25)) or ((A(25) or B_u(25)) and ((A(24) and B_u(24)) or ((A(24) or B_u(24)) and ((((A(23) and B_u(23)) or ((A(23) or B_u(23)) and ((A(22) and B_u(22)) or ((A(22) or B_u(22)) and ((A(21) and B_u(21)) or ((A(21) or B_u(21)) and ((A(20) and B_u(20)) or ((A(20) or B_u(20)) and ((((A(19) and B_u(19)) or ((A(19) or B_u(19)) and ((A(18) and B_u(18)) or ((A(18) or B_u(18)) and ((A(17) and B_u(17)) or ((A(17) or B_u(17)) and ((A(16) and B_u(16)) or ((A(16) or B_u(16)) and ((((A(15) and B_u(15)) or ((A(15) or B_u(15)) and ((A(14) and B_u(14)) or ((A(14) or B_u(14)) and ((A(13) and B_u(13)) or ((A(13) or B_u(13)) and ((A(12) and B_u(12)) or ((A(12) or B_u(12)) and ((((A(11) and B_u(11)) or ((A(11) or B_u(11)) and ((A(10) and B_u(10)) or ((A(10) or B_u(10)) and ((A(9) and B_u(9)) or ((A(9) or B_u(9)) and ((A(8) and B_u(8)) or ((A(8) or B_u(8)) and ((((A(7) and B_u(7)) or ((A(7) or B_u(7)) and ((A(6) and B_u(6)) or ((A(6) or B_u(6)) and ((A(5) and B_u(5)) or ((A(5) or B_u(5)) and ((A(4) and B_u(4)) or ((A(4) or B_u(4)) and ((((A(3) and B_u(3)) or ((A(3) or B_u(3)) and ((A(2) and B_u(2)) or ((A(2) or B_u(2)) and ((A(1) and B_u(1)) or ((A(1) or B_u(1)) and ((A(0) and B_u(0)) or ((A(0) or B_u(0)) and (mode))))))))) and control(0)) or (mode and (not control(0)))))))))))) and control(1)) or (mode and (not control(1)))))))))))) and control(0)) or (mode and (not control(0)))))))))))) and control(2)) or (mode and (not control(2)))))))))))) and control(0)) or (mode and (not control(0)))))))))))) and control(1)) or (mode and (not control(1)))))))))))) and control(0)) or (mode and (not control(0)))))))));

end process Carrys;
process(A,B_u,C)
    begin
    for n in 0 to 31 loop
      S(n) <= (A(n)xor B_u(n)) xor C(n);
    end loop;
    end process;
end TypeArchitecture;

// VHDL entity ALU, as the project stores it:
--------------------------------------------------------------------------------
-- Project :
-- File    :
-- Autor   :
-- Date    :
--
--------------------------------------------------------------------------------
-- Description :
--
--------------------------------------------------------------------------------

LIBRARY ieee;
USE ieee.std_logic_1164.all;
use ieee.numeric_std.all;

ENTITY ALU IS
  PORT (
    a,b      : IN  std_logic_vector(31 DOWNTO 0);
    op        : IN  std_logic_vector(3 DOWNTO 0);
    r_select, mode        : OUT std_logic;
    r,ae,be        : OUT std_logic_vector(31 DOWNTO 0);
    vec_size : IN std_logic_vector(1 DOWNTO 0)
    );
END ALU;

--------------------------------------------------------------------------------
--Complete your VHDL description below
--------------------------------------------------------------------------------

ARCHITECTURE TypeArchitecture OF ALU IS

SIGNAL b_i : integer;
SIGNAL b_2i : integer;
SIGNAL b_3i : integer;
SIGNAL b_4i : integer;
SIGNAL b_5i : integer;
SIGNAL b_6i : integer;
SIGNAL b_7i : integer;
SIGNAL b_8i : integer;
BEGIN

PROCESS(a,b,op,b_i,b_2i,b_3i,b_4i,b_5i,b_6i,b_7i,b_8i)
BEGIN
case op is
when "0000" => --AND
	r <= a AND b;
	r_select <= '0';
when "0001" => --OR
	r <= a OR b;
	r_select <= '0';
when "0111" => --XOR
	r <= a XOR b;
	r_select <= '0';
when "0010" => --Soma
	ae <= a;
	be <= b;
	r_select <= '1';
	mode <= '0';
when "0110" => --Sub
	ae <= a;
	be <= b;
	r_select <= '1';
	mode <= '1';
when "1000"=> --Shift Left
	
	if(vec_size = "10") then
	b_2i <= to_integer(unsigned(b(31 downto 16)));
	b_i <= to_integer(unsigned(b(15 downto 0)));
	r(31 downto 16) <= std_logic_vector(shift_left(unsigned(a(31 DOWNTO 16)), b_2i));
	r(15 downto 0) <= std_logic_vector(shift_left(unsigned(a(15 DOWNTO 0)), b_i));
	r_select <= '0';
     elsif(vec_size="01")then
     b_4i <= to_integer(unsigned(b(31 downto 24)));
	b_3i <= to_integer(unsigned(b(23 downto 16)));
	b_2i <= to_integer(unsigned(b(15 downto 8)));
	b_i <= to_integer(unsigned(b(7 downto 0)));
	
	r(31 downto 24) <= std_logic_vector(shift_left(unsigned(a(31 DOWNTO 24)), b_4i));
	r(23 downto 16) <= std_logic_vector(shift_left(unsigned(a(23 DOWNTO 16)), b_3i));
	r(15 downto 8)  <= std_logic_vector(shift_left(unsigned(a(15 DOWNTO 8)), b_2i));
	r(7 downto 0)   <= std_logic_vector(shift_left(unsigned(a(7 DOWNTO 0)), b_i));
	r_select <= '0';
	elsif(vec_size="00")then
	b_8i <= to_integer(unsigned(b(31 downto 28)));
	b_7i <= to_integer(unsigned(b(27 downto 24)));
	b_6i <= to_integer(unsigned(b(23 downto 20)));
	b_5i <= to_integer(unsigned(b(19 downto 16)));
	b_4i <= to_integer(unsigned(b(15 downto 12)));
	b_3i <= to_integer(unsigned(b(11 downto 8)));
	b_2i <= to_integer(unsigned(b(7 downto 4)));
	b_i <= to_integer(unsigned(b(3 downto 0)));
	
	r(31 downto 28) <= std_logic_vector(shift_left(unsigned(a(31 DOWNTO 28)), b_8i));
	r(27 downto 24) <= std_logic_vector(shift_left(unsigned(a(27 DOWNTO 24)), b_7i));
	r(23 downto 20)  <= std_logic_vector(shift_left(unsigned(a(23 DOWNTO 20)), b_6i));
	r(19 downto 16)   <= std_logic_vector(shift_left(unsigned(a(19 DOWNTO 16)), b_5i));
	r(15 downto 12) <= std_logic_vector(shift_left(unsigned(a(15 DOWNTO 12)), b_4i));
	r(11 downto 8) <= std_logic_vector(shift_left(unsigned(a(11 DOWNTO 8)), b_3i));
	r(7 downto 4)  <= std_logic_vector(shift_left(unsigned(a(7 DOWNTO 4)), b_2i));
	r(3 downto 0)   <= std_logic_vector(shift_left(unsigned(a(3 DOWNTO 0)), b_i));
	r_select <= '0';
	else
	b_i <= to_integer(unsigned(b));
	r <= std_logic_vector(shift_left(unsigned(a), b_i));
	r_select <= '0';
	end if;
	
when "1001"=> --Shift Right
	
	if(vec_size = "10") then
	b_2i <= to_integer(unsigned(b(31 downto 16)));
	b_i <= to_integer(unsigned(b(15 downto 0)));
	r(31 downto 16) <= std_logic_vector(shift_right(unsigned(a(31 DOWNTO 16)), b_2i));
	r(15 downto 0) <= std_logic_vector(shift_right(unsigned(a(15 DOWNTO 0)), b_i));
	r_select <= '0';
     elsif(vec_size="01")then
     b_4i <= to_integer(unsigned(b(31 downto 24)));
	b_3i <= to_integer(unsigned(b(23 downto 16)));
	b_2i <= to_integer(unsigned(b(15 downto 8)));
	b_i <= to_integer(unsigned(b(7 downto 0)));
	
	r(31 downto 24) <= std_logic_vector(shift_right(unsigned(a(31 DOWNTO 24)), b_4i));
	r(23 downto 16) <= std_logic_vector(shift_right(unsigned(a(23 DOWNTO 16)), b_3i));
	r(15 downto 8)  <= std_logic_vector(shift_right(unsigned(a(15 DOWNTO 8)), b_2i));
	r(7 downto 0)   <= std_logic_vector(shift_right(unsigned(a(7 DOWNTO 0)), b_i));
	r_select <= '0';
	elsif(vec_size="00")then
	b_8i <= to_integer(unsigned(b(31 downto 28)));
	b_7i <= to_integer(unsigned(b(27 downto 24)));
	b_6i <= to_integer(unsigned(b(23 downto 20)));
	b_5i <= to_integer(unsigned(b(19 downto 16)));
	b_4i <= to_integer(unsigned(b(15 downto 12)));
	b_3i <= to_integer(unsigned(b(11 downto 8)));
	b_2i <= to_integer(unsigned(b(7 downto 4)));
	b_i <= to_integer(unsigned(b(3 downto 0)));
	
	r(31 downto 28) <= std_logic_vector(shift_right(unsigned(a(31 DOWNTO 28)), b_8i));
	r(27 downto 24) <= std_logic_vector(shift_right(unsigned(a(27 DOWNTO 24)), b_7i));
	r(23 downto 20)  <= std_logic_vector(shift_right(unsigned(a(23 DOWNTO 20)), b_6i));
	r(19 downto 16)   <= std_logic_vector(shift_right(unsigned(a(19 DOWNTO 16)), b_5i));
	r(15 downto 12) <= std_logic_vector(shift_right(unsigned(a(15 DOWNTO 12)), b_4i));
	r(11 downto 8) <= std_logic_vector(shift_right(unsigned(a(11 DOWNTO 8)), b_3i));
	r(7 downto 4)  <= std_logic_vector(shift_right(unsigned(a(7 DOWNTO 4)), b_2i));
	r(3 downto 0)   <= std_logic_vector(shift_right(unsigned(a(3 DOWNTO 0)), b_i));
	r_select <= '0';
	else
	b_i <= to_integer(unsigned(b));
	r <= std_logic_vector(shift_right(unsigned(a), b_i));
	r_select <= '0';
	end if;


when others =>
	ae <= a;
	be <= b;
	r_select <= '1';
	mode <= '1';
END case;
END PROCESS;
END TypeArchitecture;

// VHDL entity zero_analyzer, as the project stores it:
--------------------------------------------------------------------------------
-- Project :
-- File    :
-- Autor   :
-- Date    :
--
--------------------------------------------------------------------------------
-- Description :
--
--------------------------------------------------------------------------------

LIBRARY ieee;
USE ieee.std_logic_1164.all;

ENTITY zero_analyzer IS
  PORT (
    r        : IN  std_logic_vector(31 DOWNTO 0);
    zero       : OUT std_logic
    );
END zero_analyzer;
ARCHITECTURE TypeArchitecture OF zero_analyzer IS

BEGIN

process(r)
BEGIN

IF (r = "00000000000000000000000000000000") THEN
	zero <= '1';
ELSE
	zero <= '0';
END IF;
END PROCESS;

END TypeArchitecture;

// VHDL entity ALU_ctrl, as the project stores it:
--------------------------------------------------------------------------------
-- Project :
-- File    :
-- Autor   :
-- Date    :
--
--------------------------------------------------------------------------------
-- Description :
--
--------------------------------------------------------------------------------

LIBRARY ieee;
USE ieee.std_logic_1164.all;

ENTITY ALU_ctrl IS
  PORT (
    func7      : IN  std_logic;
    func3        : IN  std_logic_vector(2 DOWNTO 0);
    aluop : IN std_logic_vector(1 DOWNTO 0);
    aluctrl        : OUT std_logic_vector(3 DOWNTO 0)
    );
END ALU_ctrl;

ARCHITECTURE TypeArchitecture OF ALU_ctrl IS
BEGIN
PROCESS (func7,func3,aluop)
BEGIN
IF (aluop = "00") THEN
	aluctrl <= "0010";
ELSIF (aluop = "01") THEN
	aluctrl <= "0110";
ELSIF (aluop = "10") THEN
	IF (func7 = '1') THEN
		aluctrl <= "0110";
	ELSIF (func7 = '0') THEN
		IF (func3 = "000") THEN
			aluctrl <= "0010";
		ELSIF (func3 = "111") THEN
			aluctrl <= "0000";
		ELSIF (func3 = "110") THEN
			aluctrl <= "0001";
		ELSIF (func3 = "001") THEN
			aluctrl <= "1000";
		ELSIF (func3 = "101") THEN
			aluctrl <= "1001";
		ELSIF (func3 = "100") THEN
			aluctrl <= "0111";
		END IF;
	END IF;
END IF;
END PROCESS;

END TypeArchitecture;

// VHDL entity ID_EX, as the project stores it:
--------------------------------------------------------------------------------
-- Project :
-- File    :
-- Autor   :
-- Date    :
--
--------------------------------------------------------------------------------
-- Description :
--
--------------------------------------------------------------------------------

LIBRARY ieee;
USE ieee.std_logic_1164.all;

ENTITY ID_EX IS
  PORT (
    clock      : IN  std_logic;
    imm,rd1,rd2,pc        : IN  std_logic_vector(31 DOWNTO 0);
    func3: IN std_logic_vector (2 DOWNTO 0);
    rw: IN std_logic_vector(4 DOWNTO 0);
    regwrite, alusrc, memread, memwrite, memtoreg, lui : IN std_logic;
    aluop,branch       : IN std_logic_vector(1 DOWNTO 0);
    func7 : IN std_logic;
    ra1,ra2 : IN std_logic_vector (4 DOWNTO 0);
    flush : IN std_logic;
    vec_size : IN std_logic_vector (1 DOWNTO 0);
    pcnext : IN std_logic_vector (31 DOWNTO 0);
    imm_o,rd1_o,rd2_o,pc_o        : OUT  std_logic_vector(31 DOWNTO 0);
    func3_o: OUT std_logic_vector (2 DOWNTO 0);
    rw_o: OUT std_logic_vector(4 DOWNTO 0);
    regwrite_o, alusrc_o, memread_o, memwrite_o, memtoreg_o, lui_o : OUT std_logic;
    aluop_o,branch_o       : OUT std_logic_vector(1 DOWNTO 0);
    func7_o : OUT std_logic;
    ra1_o, ra2_o : OUT std_logic_vector (4 DOWNTO 0);
    vec_size_o : OUT std_logic_vector (1 DOWNTO 0);
    pcnext_o : OUT std_logic_vector (31 DOWNTO 0)
    );
END ID_EX;

--------------------------------------------------------------------------------
--Complete your VHDL description below
--------------------------------------------------------------------------------

ARCHITECTURE TypeArchitecture OF ID_EX IS
SIGNAL imm_mem,rd1_mem,rd2_mem,pc_mem, pcnext_mem : std_logic_vector (31 DOWNTO 0);
SIGNAL func3_mem : std_logic_vector (2 DOWNTO 0);
SIGNAL rw_mem : std_logic_vector (4 DOWNTO 0);
SIGNAL regwrite_mem, alusrc_mem, memread_mem, memwrite_mem, memtoreg_mem, lui_mem, func7_mem :std_logic;
SIGNAL aluop_mem, branch_mem : std_logic_vector(1 DOWNTO 0);
SIGNAL ra1_mem, ra2_mem : std_logic_vector(4 DOWNTO 0);
SIGNAL vec_size_mem : std_logic_vector (1 DOWNTO 0);
BEGIN
PROCESS(clock, imm, rd1, rd2, pc, func3, rw, regwrite, alusrc, memread, memwrite, memtoreg, lui, aluop, branch, func7,flush, vec_size)
BEGIN
IF (rising_edge(clock)) THEN
	imm_mem <= imm;
	rd1_mem <= rd1;
	rd2_mem <= rd2;
	pc_mem <= pc;
	func3_mem <= func3;
	rw_mem <= rw;
	regwrite_mem <= regwrite;
	alusrc_mem <= alusrc;
	memread_mem <= memread;
	memwrite_mem <= memwrite;
	memtoreg_mem <= memtoreg;
	lui_mem <= lui;
	aluop_mem <= aluop;
	branch_mem <= branch;
	func7_mem <= func7;
	ra1_mem <= ra1;
	ra2_mem <= ra2;
	vec_size_mem <= vec_size;
	pcnext_mem <= pcnext;
END IF;
IF(falling_edge(clock)) THEN
	IF (flush = '1') THEN
		imm_o <= imm;
		rd1_o <= rd1;
		rd2_o <= rd2;
		pc_o <= pc;
		func3_o <= func3;
		rw_o <= rw;
		regwrite_o <= '0';
		alusrc_o <= '0';
		memread_o <= '0';
		memwrite_o <= '0';
		memtoreg_o <= '0';
		lui_o <= '0';
		aluop_o <= "00";
		branch_o <= "00";
		func7_o <= func7;
		ra1_o <= ra1;
		ra2_o <= ra2;
		vec_size_o <= vec_size;
		pcnext_o <= pcnext;
	ELSE
			imm_o <= imm_mem;
			rd1_o <= rd1_mem;
			rd2_o <= rd2_mem;
			pc_o <= pc_mem;
			func3_o <= func3_mem;
			rw_o <= rw_mem;
			regwrite_o <= regwrite_mem;
			alusrc_o <= alusrc_mem;
			memread_o <= memread_mem;
			memwrite_o <= memwrite_mem;
			memtoreg_o <= memtoreg_mem;
			lui_o <= lui_mem;
			aluop_o <= aluop_mem;
			branch_o <= branch_mem;
			func7_o <= func7_mem;
			ra1_o <= ra1_mem;
			ra2_o <= ra2_mem;
			vec_size_o <= vec_size_mem;
			pcnext_o <= pcnext_mem;
	END IF;
END IF;
END PROCESS;

END TypeArchitecture;

// VHDL entity EX_MEM, as the project stores it:
--------------------------------------------------------------------------------
-- Project :
-- File    :
-- Autor   :
-- Date    :
--
--------------------------------------------------------------------------------
-- Description :
--
--------------------------------------------------------------------------------

LIBRARY ieee;
USE ieee.std_logic_1164.all;

ENTITY EX_MEM IS
  PORT (

    clock      : IN  std_logic;
    branch_res, alu_res, rd2        : IN  std_logic_vector(31 DOWNTO 0);
    rw : IN std_logic_vector(4 DOWNTO 0);
    regwrite, memread, memwrite, memtoreg, zero : IN std_logic;
    branch : IN std_logic_vector(1 DOWNTO 0);
    flush : IN std_logic;
    branch_res_o, alu_res_o, rd2_o        : OUT  std_logic_vector(31 DOWNTO 0);
    rw_o : OUT std_logic_vector(4 DOWNTO 0);
    regwrite_o, memread_o, memwrite_o, memtoreg_o, zero_o : OUT std_logic;
    branch_o : OUT std_logic_vector(1 DOWNTO 0)
    );
END EX_MEM;

--------------------------------------------------------------------------------
--Complete your VHDL description below
--------------------------------------------------------------------------------

ARCHITECTURE TypeArchitecture OF EX_MEM IS
SIGNAL branch_res_mem, alu_res_mem, rd2_mem : std_logic_vector(31 DOWNTO 0);
SIGNAL rw_mem : std_logic_vector(4 DOWNTO 0);
SIGNAL regwrite_mem, memread_mem, memwrite_mem, memtoreg_mem, zero_mem : std_logic;
Signal branch_mem : std_logic_vector(1 DOWNTO 0);
BEGIN
PROCESS(clock, branch_res, alu_res, zero, rd2, rw, regwrite, memread, memwrite, memtoreg, branch,flush)
BEGIN
	IF (rising_edge(clock)) THEN
		branch_res_mem <= branch_res;
		alu_res_mem <= alu_res;
		zero_mem <= zero;
		rd2_mem <= rd2;
		rw_mem <= rw;
		regwrite_mem <= regwrite;
		memread_mem <= memread;
		memwrite_mem <= memwrite;
		memtoreg_mem <= memtoreg;
		branch_mem <= branch;
	END IF;
	IF(falling_edge(clock)) THEN 
		IF (flush = '1') THEN
			branch_res_o <= branch_res;
			alu_res_o <= alu_res;
			zero_o <= zero;
			rd2_o <= rd2;
			rw_o <= rw;
			regwrite_o <= '0';
			memread_o <= '0';
			memwrite_o <= '0';
			memtoreg_o <= '0';
			branch_o <= "00";
		ELSE
			branch_res_o <= branch_res_mem;
			alu_res_o <= alu_res_mem;
			zero_o <= zero_mem;
			rw_o <= rw_mem;
			regwrite_o <= regwrite_mem;
			memread_o <= memread_mem;
			memwrite_o <= memwrite_mem;
			memtoreg_o <= memtoreg_mem;
			branch_o <= branch_mem;
			IF (rd2_mem = "UUUUUUUUUUUUUUUUUUUUUUUUUUUUUUUU") THEN
				rd2_o <= "00000000000000000000000000000000";
			ELSE
				rd2_o <= rd2_mem;
			END IF;
		END IF;

	END IF;
END PROCESS;
END TypeArchitecture;

// VHDL entity MEM_WB, as the project stores it:
--------------------------------------------------------------------------------
-- Project :
-- File    :
-- Autor   :
-- Date    :
--
--------------------------------------------------------------------------------
-- Description :
--
--------------------------------------------------------------------------------

LIBRARY ieee;
USE ieee.std_logic_1164.all;

ENTITY MEM_WB IS
  PORT (

    clock      : IN  std_logic;
    rdm, alu_res        : IN  std_logic_vector(31 DOWNTO 0);
    regwrite, memtoreg : IN std_logic;
    rw : IN std_logic_vector (4 DOWNTO 0);
    rdm_o, alu_res_o: OUT std_logic_vector (31 DOWNTO 0);
    regwrite_o, memtoreg_o : OUT std_logic;
    rw_o : OUT std_logic_vector (4 DOWNTO 0)
    
    );
END MEM_WB;

--------------------------------------------------------------------------------
--Complete your VHDL description below
--------------------------------------------------------------------------------

ARCHITECTURE TypeArchitecture OF MEM_WB IS
SIGNAL rdm_mem, alu_res_mem : std_logic_vector(31 DOWNTO 0);
SIGNAL regwrite_mem, memtoreg_mem : std_logic;
SIGNAL rw_mem : std_logic_vector (4 DOWNTO 0);
BEGIN
PROCESS (rdm, alu_res, regwrite, memtoreg, rw,clock)
BEGIN
IF (rising_edge(clock)) THEN 
	rdm_mem <= rdm;
	alu_res_mem <= alu_res;
	regwrite_mem <= regwrite;
	memtoreg_mem <= memtoreg;
	rw_mem <= rw;
END IF;
IF (falling_edge(clock)) THEN 
	rdm_o <= rdm_mem;
	alu_res_o <= alu_res_mem;
	regwrite_o <= regwrite_mem;
	memtoreg_o <= memtoreg_mem;
	rw_o <= rw_mem;
END IF;
END PROCESS;
END TypeArchitecture;
// VHDL entity Reg_file, as the project stores it:
--------------------------------------------------------------------------------
-- Project :
-- File    :
-- Autor   :
-- Date    :
--
--------------------------------------------------------------------------------
-- Description :
--
--------------------------------------------------------------------------------

LIBRARY ieee;
USE ieee.std_logic_1164.all;
USE ieee.numeric_std.all;

ENTITY Reg_file IS
  PORT (
    clock,write_e, reset      : IN  std_logic;
    rd1a,rd2a,rwa,manual_address : IN std_logic_vector(4 DOWNTO 0);
    rw : IN std_logic_vector (31 DOWNTO 0);

    rd1,rd2, manual_value        : OUT std_logic_vector(31 DOWNTO 0)
    );
END Reg_file;

--------------------------------------------------------------------------------
--Complete your VHDL description below
--------------------------------------------------------------------------------

ARCHITECTURE TypeArchitecture OF Reg_file IS
TYPE register_file is array(0 to 31) of std_logic_vector(31 DOWNTO 0);
SIGNAL registers : register_file := 
   ("00000000000000000000000000000000","00000000000000000000000000001000","00000000000000000000000000000010","00000000000000000000000000000000",
    "00000000000000000000000000000000","00000000000000000000000000000000","00000000000000000000000000000000","00000000000000000000000000000000",
    "00000000000000000000000000000000","00000000000000000000000000000000","00000000000000000000000000000001","00000000000000000000000000000000",
    "00000000000000000000000000000000","00000000000000000000000000000000","00000000000000000000000000000000","00000000000000000000000000000000",
    "00000000000000000000000000000000","00000000000000000000000000000000","00000000000000000000000000000000","00000000000000000000000000000000",
    "00000000000000000000000000000000","00000000000000000000000000000000","00000000000000000000000000000000","00000000000000000000000000000000",
    "00000000000000000000000000000000","00000000000000000000000000000000","00000000000000000000000000000000","00000000000000000000000000000000",
    "00000000000000000000000000000000","00000000000000000000000000000000","00000000000000000000000000000000","00000000000000000000000000000000");
BEGIN
process (clock, write_e, reset, registers, rd1a, rd2a, rwa, rw, manual_address)
BEGIN
manual_value <= registers(to_integer(unsigned(manual_address)));
IF (1 = 1) THEN
	rd1 <= registers(to_integer(unsigned(rd1a)));
	rd2 <= registers(to_integer(unsigned(rd2a)));
	IF (write_e = '1' AND to_integer(unsigned(rwa)) /= 0) THEN --Can't write on register X0
		registers(to_integer(unsigned(rwa))) <= rw;
	END IF;
END IF;
IF (reset = '1') THEN --Wipes all registers
	registers <= 
   ("00000000000000000000000000000000","00000000000000000000000000000000","00000000000000000000000000000000","00000000000000000000000000000000",
    "00000000000000000000000000000000","00000000000000000000000000000000","00000000000000000000000000000000","00000000000000000000000000000000",
    "00000000000000000000000000000000","00000000000000000000000000000000","00000000000000000000000000000000","00000000000000000000000000000000",
    "00000000000000000000000000000000","00000000000000000000000000000000","00000000000000000000000000000001","00000000000000000000000000000000",
    "00000000000000000000000000000000","00000000000000000000000000000000","00000000000000000000000000000000","00000000000000000000000000000000",
    "00000000000000000000000000000000","00000000000000000000000000000000","00000000000000000000000000000000","00000000000000000000000000000000",
    "00000000000000000000000000000000","00000000000000000000000000000000","00000000000000000000000000000000","00000000000000000000000000000000",
    "00000000000000000000000000000000","00000000000000000000000000000000","00000000000000000000000000000000","00000000000000000000000000000000");
END IF;
END PROCESS;
END TypeArchitecture;

// VHDL entity Forwarding_unit, as the project stores it:
--------------------------------------------------------------------------------
-- Project :
-- File    :
-- Autor   :
-- Date    :
--
--------------------------------------------------------------------------------
-- Description :
--
--------------------------------------------------------------------------------

LIBRARY ieee;
USE ieee.std_logic_1164.all;

ENTITY Forwarding_unit IS
  PORT (
    regwriteex,regwritemem    : IN  std_logic;
    pcra1, pcra2, pcradex, pcradmem       : IN  std_logic_vector(4 DOWNTO 0);
    fora,forb        : OUT std_logic_vector(1 DOWNTO 0) --00 register, 01 memory result, 10 alu result
    );
END Forwarding_unit;

--------------------------------------------------------------------------------
--Complete your VHDL description below
--------------------------------------------------------------------------------

ARCHITECTURE TypeArchitecture OF Forwarding_unit IS

BEGIN
process(regwriteex, regwritemem, pcra1, pcra2, pcradex, pcradmem)
BEGIN
fora <= "00";
forb <= "00";
IF (regwritemem = '1' AND pcradmem /= "00000") THEN
	IF (pcra1 = pcradmem) THEN
		fora <= "01";
	END IF;
	IF (pcra2 = pcradmem AND pcradmem /= "00000") THEN
		forb <= "01";
	END IF;
END IF;
IF (regwriteex = '1') THEN
	IF (pcra1 = pcradex AND pcradex /=  "00000") THEN
		fora <= "10";
	END IF;
	IF (pcra2 = pcradex AND pcradex /= "00000") THEN
		forb <= "10";
	END IF;
END IF;
END PROCESS;
END TypeArchitecture;

// VHDL entity Hazard_unit, as the project stores it:
--------------------------------------------------------------------------------
-- Project :
-- File    :
-- Autor   :
-- Date    :
--
--------------------------------------------------------------------------------
-- Description :
--
--------------------------------------------------------------------------------

LIBRARY ieee;
USE ieee.std_logic_1164.all;

ENTITY Hazard_unit IS
  PORT (
    idexmemread      : IN  std_logic;
    rwa, rda1, rda2 : IN std_logic_vector(4 DOWNTO 0);
    branch : IN std_logic;
    pcwrite, ifidwrite, nop, flush : OUT std_logic
    );
END Hazard_unit;

--------------------------------------------------------------------------------
--Complete your VHDL description below
--------------------------------------------------------------------------------

ARCHITECTURE TypeArchitecture OF Hazard_unit IS

BEGIN
process (idexmemread, rwa, rda1, rda2,branch)
BEGIN
IF (idexmemread = '1') THEN
	IF (rwa = rda1 OR rwa = rda2) THEN
		pcwrite <= '0';
		ifidwrite <= '0';
		nop <= '1';
	ELSE
		pcwrite <= '1';
		ifidwrite <= '1';
		nop <= '0';
	END IF;
ELSE
	pcwrite <= '1';
	ifidwrite <= '1';
	nop <= '0';
END IF;
IF (branch = '1') THEN
	flush <= '1';
ELSE
	flush <= '0';
END IF;
END PROCESS;
END TypeArchitecture;

// VHDL entity RegAdress_Validator, as the project stores it:
--------------------------------------------------------------------------------
-- Project :
-- File    :
-- Autor   :
-- Date    :
--
--------------------------------------------------------------------------------
-- Description :
--
--------------------------------------------------------------------------------

LIBRARY ieee;
USE ieee.std_logic_1164.all;

ENTITY RegAdress_Validator IS
  PORT (

    ra1,ra2     : IN  std_logic_vector(4 DOWNTO 0);
    opcode        : IN  std_logic_vector(6 DOWNTO 0);
    ra1_o,ra2_o        : OUT std_logic_vector(4 DOWNTO 0)
    );
END RegAdress_Validator;

--------------------------------------------------------------------------------
--Complete your VHDL description below
--------------------------------------------------------------------------------

ARCHITECTURE TypeArchitecture OF RegAdress_Validator IS

BEGIN
PROCESS (ra1,ra2,opcode)
BEGIN 
IF (opcode = "0110011" OR opcode = "0100011" OR opcode = "1100011" OR opcode = "0110000" OR opcode = "0110001" OR opcode = "0110010") THEN --Há reg 2 e reg 1
	ra2_o <= ra2;
	ra1_o <= ra1;
ELSIF (opcode = "0000011" OR opcode = "0010011" OR opcode = "0010000" OR opcode = "0010001" OR opcode = "0010010") THEN --Só há reg 1
	ra2_o <= "00000";
	ra1_o <= ra1;
ELSE --Não há nenhum reg
	ra2_o <= "00000";
	ra1_o <= "00000";
END IF;
END PROCESS;
END TypeArchitecture;
